// Logisim project compat_lab1.circ as structural Verilog: 5 circuits, main circuit HalfAdder_1Bit
module HalfAdder_1Bit (
  input  A,
  input  B,
  output S,
  output C
);

  xor xor_1 (S, A, B);
  and and_1 (C, B, A);
endmodule

module FullAdder_1Bit (
  input  A,
  input  B,
  input  Cin,
  output S,
  output Cout
);

  wire and_1_out, and_2_out, xor_1_out;

  xor xor_1 (xor_1_out, A, B);
  and and_1 (and_1_out, xor_1_out, Cin);
  and and_2 (and_2_out, A, B);
  xor xor_2 (S, xor_1_out, Cin);
  or or_1 (Cout, and_1_out, and_2_out);
endmodule

module RCA_4Bits (
  input  A3,
  input  B3,
  input  A2,
  input  B2,
  input  A1,
  input  B1,
  input  A0,
  input  B0,
  input  C0,
  output C4,
  output S3,
  output S2,
  output S1,
  output S0
);

  wire fulladder_1bit_2_cout, fulladder_1bit_3_cout, fulladder_1bit_4_cout;

  FullAdder_1Bit fulladder_1bit_1 (.S(S3), .Cout(C4), .A(A3), .B(B3), .Cin(fulladder_1bit_2_cout));
  FullAdder_1Bit fulladder_1bit_2 (.S(S2), .Cout(fulladder_1bit_2_cout), .A(A2), .B(B2), .Cin(fulladder_1bit_3_cout));
  FullAdder_1Bit fulladder_1bit_3 (.S(S1), .Cout(fulladder_1bit_3_cout), .A(A1), .B(B1), .Cin(fulladder_1bit_4_cout));
  FullAdder_1Bit fulladder_1bit_4 (.S(S0), .Cout(fulladder_1bit_4_cout), .A(A0), .B(B0), .Cin(C0));
endmodule

module CLA_4Bits (
  input  A3,
  input  B3,
  input  A2,
  input  B2,
  input  A1,
  input  B1,
  input  A0,
  input  B0,
  input  C0,
  output C4,
  output S3,
  output S2,
  output S1,
  output S0
);

  wire and_1_out, and_2_out, and_3_out, and_4_out, and_5_out, and_6_out, and_7_out, and_8_out, and_9_out,
       and_10_out, C1_out, C2_out, C3_out, G0_out, G1_out, G2_out, G3_out, P0_out, P1_out, P2_out, P3_out;

  and G3 (G3_out, A3, B3);
  xor P3 (P3_out, A3, B3);
  and G2 (G2_out, A2, B2);
  xor P2 (P2_out, A2, B2);
  and G1 (G1_out, A1, B1);
  xor P1 (P1_out, A1, B1);
  and G0 (G0_out, A0, B0);
  xor P0 (P0_out, A0, B0);
  and and_1 (and_1_out, P3_out, P2_out, G1_out);
  and and_2 (and_2_out, P2_out, G1_out);
  and and_3 (and_3_out, P1_out, G0_out);
  and and_4 (and_4_out, P1_out, P0_out, C0);
  and and_5 (and_5_out, P0_out, C0);
  xor xor_1 (S0, P0_out, C0);
  and and_6 (and_6_out, P3_out, P2_out, P1_out, P0_out, C0);
  and and_7 (and_7_out, P3_out, P2_out, P1_out, G0_out);
  and and_8 (and_8_out, P2_out, P1_out, P0_out, C0);
  and and_9 (and_9_out, P2_out, P1_out, G0_out);
  or C2 (C2_out, G1_out, and_3_out, and_4_out);
  or C1 (C1_out, G0_out, and_5_out);
  and and_10 (and_10_out, P3_out, G2_out);
  or C3 (C3_out, and_8_out, and_9_out, G2_out, and_2_out);
  xor xor_2 (S2, P2_out, C2_out);
  xor xor_3 (S1, P1_out, C1_out);
  or or_1 (C4, and_6_out, and_7_out, and_1_out, and_10_out, G3_out);
  xor xor_4 (S3, P3_out, C3_out);
endmodule

module CLA4Bits_Test (
  input  in_1,
  input  in_2,
  input  in_3,
  input  in_4,
  input  in_5,
  input  in_6,
  input  in_7,
  input  in_8,
  input  in_9,
  output out_10,
  output out_11,
  output out_12,
  output out_13,
  output out_14
);

  CLA_4Bits cla_4bits_1 (
    .S0(out_13), .C4(out_14), .S3(out_10), .S2(out_11), .S1(out_12), .A0(in_9), .B0(in_5), .C0(in_1),
    .A3(in_6), .B3(in_2), .A2(in_7), .B2(in_3), .A1(in_8), .B1(in_4));
endmodule
