// Logisim project lab2.circ as structural Verilog: 10 circuits, main circuit 四位二进制可逆计数器
module CLA_4Bits (
  input  A3,
  input  B3,
  input  A2,
  input  B2,
  input  A1,
  input  B1,
  input  A0,
  input  B0,
  input  C0,
  output C4,
  output S3,
  output S2,
  output S1,
  output S0
);

  wire and_1_out, and_2_out, and_3_out, and_4_out, and_5_out, and_6_out, and_7_out, and_8_out, and_9_out,
       and_10_out, C1_out, C2_out, C3_out, G0_out, G1_out, G2_out, G3_out, P0_out, P1_out, P2_out, P3_out;

  and G3 (G3_out, A3, B3);
  xor P3 (P3_out, A3, B3);
  and G2 (G2_out, A2, B2);
  xor P2 (P2_out, A2, B2);
  and G1 (G1_out, A1, B1);
  xor P1 (P1_out, A1, B1);
  and G0 (G0_out, A0, B0);
  xor P0 (P0_out, A0, B0);
  and and_1 (and_1_out, P3_out, P2_out, G1_out);
  and and_2 (and_2_out, P2_out, G1_out);
  and and_3 (and_3_out, P1_out, G0_out);
  and and_4 (and_4_out, P1_out, P0_out, C0);
  and and_5 (and_5_out, P0_out, C0);
  xor xor_1 (S0, P0_out, C0);
  and and_6 (and_6_out, P3_out, P2_out, P1_out, P0_out, C0);
  and and_7 (and_7_out, P3_out, P2_out, P1_out, G0_out);
  and and_8 (and_8_out, P2_out, P1_out, P0_out, C0);
  and and_9 (and_9_out, P2_out, P1_out, G0_out);
  or C2 (C2_out, G1_out, and_3_out, and_4_out);
  or C1 (C1_out, G0_out, and_5_out);
  and and_10 (and_10_out, P3_out, G2_out);
  or C3 (C3_out, and_8_out, and_9_out, G2_out, and_2_out);
  xor xor_2 (S2, P2_out, C2_out);
  xor xor_3 (S1, P1_out, C1_out);
  or or_1 (C4, and_6_out, and_7_out, and_1_out, and_10_out, G3_out);
  xor xor_4 (S3, P3_out, C3_out);

  // Notes on the sheet:
  //   C0: pull=down
endmodule

module \四位二进制可逆计数器  (
  input  CP_U,
  input  CP_D,
  input  nLD,
  input  A,
  input  CLR,
  input  B,
  input  C,
  input  D,
  output Q_A,
  output Q_B,
  output Q_C,
  output Q_D
);

  wire and_1_out, and_2_out, and_3_out, and_4_out, and_5_out, and_6_out, and_7_out, and_8_out, and_9_out,
       and_10_out, and_11_out, and_12_out, and_13_out, and_14_out, d_ff_1_qn, d_ff_2_qn, d_ff_3_qn,
       d_ff_4_qn, not_1_out, not_2_out, not_3_out, or_1_out, or_2_out, or_3_out, or_4_out, or_5_out,
       or_6_out, or_7_out, or_8_out;

  not not_1 (not_1_out, CP_U);
  not not_2 (not_2_out, CP_D);
  not not_3 (not_3_out, nLD);
  or or_1 (or_1_out, not_1_out, not_2_out);
  and and_1 (and_1_out, not_3_out, ~CLR, A);  // AND_Gate
  and and_2 (and_2_out, Q_A, not_1_out);
  and and_3 (and_3_out, d_ff_1_qn, not_2_out);
  and and_4 (and_4_out, not_3_out, ~CLR, B);  // AND_Gate
  and and_5 (and_5_out, Q_A, Q_B, not_1_out);
  and and_6 (and_6_out, d_ff_1_qn, d_ff_2_qn, not_2_out);
  and and_7 (and_7_out, not_3_out, ~CLR, C);  // AND_Gate
  and and_8 (and_8_out, Q_A, Q_B, Q_C, not_1_out);
  and and_9 (and_9_out, d_ff_1_qn, d_ff_2_qn, d_ff_3_qn, not_2_out);
  and and_10 (and_10_out, not_3_out, ~CLR, D);  // AND_Gate
  and and_11 (and_11_out, not_3_out, ~and_1_out);  // AND_Gate
  or or_2 (or_2_out, and_2_out, and_3_out);
  and and_12 (and_12_out, not_3_out, ~and_4_out);  // AND_Gate
  or or_3 (or_3_out, and_5_out, and_6_out);
  and and_13 (and_13_out, not_3_out, ~and_7_out);  // AND_Gate
  or or_4 (or_4_out, and_8_out, and_9_out);
  and and_14 (and_14_out, not_3_out, ~and_10_out);  // AND_Gate
  D_Flip_Flop #(.trigger("falling")) d_ff_1 (
    .clk(or_1_out), .D(d_ff_1_qn), .Q(Q_A), .Qn(d_ff_1_qn), .preset(and_1_out), .reset(or_5_out));
  or or_5 (or_5_out, and_11_out, CLR);
  D_Flip_Flop #(.trigger("falling")) d_ff_2 (
    .clk(or_2_out), .D(d_ff_2_qn), .Q(Q_B), .Qn(d_ff_2_qn), .preset(and_4_out), .reset(or_6_out));
  or or_6 (or_6_out, and_12_out, CLR);
  D_Flip_Flop #(.trigger("falling")) d_ff_3 (
    .clk(or_3_out), .D(d_ff_3_qn), .Q(Q_C), .Qn(d_ff_3_qn), .preset(and_7_out), .reset(or_7_out));
  or or_7 (or_7_out, and_13_out, CLR);
  D_Flip_Flop #(.trigger("falling")) d_ff_4 (
    .clk(or_4_out), .D(d_ff_4_qn), .Q(Q_D), .Qn(d_ff_4_qn), .preset(and_10_out), .reset(or_8_out));
  or or_8 (or_8_out, and_14_out, CLR);
endmodule

module \四位二进制可逆计数器测试电路  (
  input  in_1,
  input  in_2,
  input  in_3,
  input  in_4,
  input  in_5,
  input  in_6,
  input  in_7,
  input  in_8,
  input  in_9,
  input  in_10,
  input  in_11,
  input  in_12,
  output out_13,
  output out_14,
  output out_15,
  output out_16,
  output out_17,
  output out_18,
  output out_19,
  output out_20
);

  wire button_1_out, button_2_out;

  Button button_1 (.out(button_1_out));
  \四位二进制可逆计数器  \u_四位二进制可逆计数器_1  (
    .CP_D(1'b1), .nLD(in_7), .A(in_6), .CLR(in_1), .B(in_5), .C(in_4), .D(in_3), .Q_A(out_16), .Q_B(out_15),
    .Q_C(out_14), .Q_D(out_13), .CP_U(button_1_out));
  Button button_2 (.out(button_2_out));
  \四位二进制可逆计数器  \u_四位二进制可逆计数器_2  (
    .CP_D(button_2_out), .nLD(in_12), .A(in_11), .CLR(in_2), .B(in_10), .C(in_9), .D(in_8), .Q_A(out_20),
    .Q_B(out_19), .Q_C(out_18), .Q_D(out_17), .CP_U(1'b1));
endmodule

module \二进制转8421码电路  (
  input  Q_D,
  input  Q_C,
  input  Q_B,
  input  Q_A,
  output H_3,
  output H_2,
  output H_1,
  output H_0,
  output L_3,
  output L_2,
  output L_1,
  output L_0
);

  wire or_1_out;

  or or_1 (or_1_out, Q_C, Q_B);
  CLA_4Bits cla_4bits_1 (
    .S1(L_1), .A2(H_0), .B2(Q_C), .A0(1'b0), .C0(1'b0), .B1(Q_B), .A3(1'b0), .S3(L_3), .S0(L_0), .B0(Q_A),
    .A1(H_0), .B3(Q_D), .S2(L_2));  // open: C4
  and and_1 (H_0, Q_D, or_1_out);

  assign H_1 = 1'b0;
  assign H_2 = 1'b0;
  assign H_3 = 1'b0;
endmodule

module \二进制转8421码测试电路  (
  input  in_1,
  input  in_2,
  input  in_3,
  input  in_4,
  output out_5,
  output out_6,
  output out_7,
  output out_8,
  output out_9,
  output out_10,
  output out_11,
  output out_12
);

  \二进制转8421码电路  \u_二进制转8421码电路_1  (
    .Q_D(in_1), .Q_C(in_2), .Q_B(in_3), .Q_A(in_4), .H_3(out_5), .H_2(out_6), .H_1(out_7), .H_0(out_8),
    .L_3(out_9), .L_2(out_10), .L_1(out_11), .L_0(out_12));
endmodule

module \显示电路  (
  input  D,
  input  C,
  input  B,
  input  A,
  output a_2,
  output b_2,
  output c_2,
  output d_2,
  output e,
  output f,
  output g
);

  wire and_1_out, and_2_out, and_3_out, and_4_out, and_5_out, and_6_out, and_7_out, and_8_out, and_9_out,
       and_10_out, and_11_out, and_12_out, and_13_out, and_14_out, and_15_out, and_16_out, and_17_out,
       and_18_out, and_19_out, and_20_out, and_21_out, and_22_out, and_23_out, and_24_out, and_25_out,
       and_26_out, not_1_out, not_2_out, not_3_out, not_4_out, not_5_out, not_6_out, not_7_out, not_8_out,
       not_9_out, not_10_out, not_11_out, not_12_out, not_13_out, not_14_out, not_15_out, not_16_out,
       not_17_out, not_18_out, not_19_out, not_20_out, not_21_out, not_22_out, not_23_out, not_24_out,
       not_25_out, not_26_out, not_27_out, not_28_out, not_29_out, not_30_out, not_31_out, not_32_out,
       not_33_out, not_34_out, not_35_out, not_36_out, not_37_out;

  not not_1 (not_1_out, D);
  and and_1 (and_1_out, not_1_out, not_2_out, not_3_out);
  not not_2 (not_2_out, C);
  not not_3 (not_3_out, A);
  not not_4 (not_4_out, D);
  not not_5 (not_5_out, C);
  and and_2 (and_2_out, not_4_out, not_5_out, B);
  not not_6 (not_6_out, D);
  and and_3 (and_3_out, not_6_out, C, A);
  not not_7 (not_7_out, C);
  and and_4 (and_4_out, D, not_7_out, not_8_out);
  not not_8 (not_8_out, B);
  and and_5 (and_5_out, D, not_9_out, A);
  not not_9 (not_9_out, B);
  not not_10 (not_10_out, D);
  and and_6 (and_6_out, not_10_out, not_11_out);
  not not_11 (not_11_out, C);
  not not_12 (not_12_out, C);
  and and_7 (and_7_out, not_12_out, not_13_out);
  not not_13 (not_13_out, B);
  not not_14 (not_14_out, B);
  and and_8 (and_8_out, not_14_out, not_15_out);
  not not_15 (not_15_out, A);
  not not_16 (not_16_out, D);
  and and_9 (and_9_out, not_16_out, B, A);
  not not_17 (not_17_out, C);
  and and_10 (and_10_out, not_17_out, not_18_out);
  not not_18 (not_18_out, B);
  not not_19 (not_19_out, C);
  and and_11 (and_11_out, not_19_out, A);
  not not_20 (not_20_out, D);
  and and_12 (and_12_out, not_20_out, C);
  not not_21 (not_21_out, C);
  and and_13 (and_13_out, not_21_out, not_22_out);
  not not_22 (not_22_out, A);
  not not_23 (not_23_out, C);
  and and_14 (and_14_out, not_23_out, B);
  and and_15 (and_15_out, B, not_24_out);
  not not_24 (not_24_out, A);
  and and_16 (and_16_out, C, not_25_out, A);
  not not_25 (not_25_out, B);
  not not_26 (not_26_out, C);
  and and_17 (and_17_out, not_26_out, not_27_out);
  not not_27 (not_27_out, A);
  and and_18 (and_18_out, B, not_28_out);
  not not_28 (not_28_out, A);
  not not_29 (not_29_out, B);
  and and_19 (and_19_out, not_29_out, not_30_out);
  not not_30 (not_30_out, A);
  and and_20 (and_20_out, C, not_31_out);
  not not_31 (not_31_out, B);
  and and_21 (and_21_out, C, not_32_out);
  not not_32 (not_32_out, A);
  and and_22 (and_22_out, D, not_33_out);
  not not_33 (not_33_out, B);
  not not_34 (not_34_out, C);
  and and_23 (and_23_out, not_34_out, B);
  and and_24 (and_24_out, C, not_35_out);
  not not_35 (not_35_out, B);
  and and_25 (and_25_out, C, not_36_out);
  not not_36 (not_36_out, A);
  and and_26 (and_26_out, D, not_37_out);
  not not_37 (not_37_out, C);
  or or_1 (a_2, and_1_out, and_2_out, and_3_out, and_4_out, and_5_out);
  or or_2 (b_2, and_6_out, and_7_out, and_8_out, and_9_out);
  or or_3 (c_2, and_10_out, and_11_out, and_12_out);
  or or_4 (d_2, and_13_out, and_14_out, and_15_out, and_16_out);
  or or_5 (e, and_17_out, and_18_out);
  or or_6 (f, and_19_out, and_20_out, and_21_out, and_22_out);
  or or_7 (g, and_23_out, and_24_out, and_25_out, and_26_out);
endmodule

module \显示电路测试电路  (
  input  in_1,
  input  in_2,
  input  in_3,
  input  in_4
);

  wire \显示电路_1_a_2 , \显示电路_1_b_2 , \显示电路_1_c_2 , \显示电路_1_d_2 , \显示电路_1_e , \显示电路_1_f , \显示电路_1_g ;

  \显示电路  \u_显示电路_1  (
    .D(in_4), .C(in_3), .B(in_2), .A(in_1), .a_2(\显示电路_1_a_2 ), .b_2(\显示电路_1_b_2 ), .c_2(\显示电路_1_c_2 ),
    .d_2(\显示电路_1_d_2 ), .e(\显示电路_1_e ), .f(\显示电路_1_f ), .g(\显示电路_1_g ));
  _7_Segment_Display u_7_segment_display_1 (
    .g(\显示电路_1_g ), .f(\显示电路_1_f ), .a(\显示电路_1_a_2 ), .b(\显示电路_1_b_2 ), .e(\显示电路_1_e ), .d(\显示电路_1_d_2 ),
    .c(\显示电路_1_c_2 ), .dp(1'b0));
endmodule

module \报警电路  (
  input  CP_prime__U,
  input  in_2,
  input  CP_prime__D,
  input  in_4,
  input  in_5,
  input  in_6,
  input  in_7,
  input  in_8,
  output WARN,
  output out_10,
  output out_11,
  output out_12,
  output out_13
);

  wire and_2_out, nand_1_out, nand_2_out, or_1_out;

  or or_1 (or_1_out, out_13, out_12, out_11, out_10);
  and and_1 (WARN, CP_prime__U, and_2_out);
  and and_2 (and_2_out, out_13, out_12, out_11, out_10);
  nand nand_1 (nand_1_out, ~and_2_out, CP_prime__U);  // NAND_Gate
  nand nand_2 (nand_2_out, or_1_out, CP_prime__D);
  \四位二进制可逆计数器  \u_四位二进制可逆计数器_1  (
    .CP_D(nand_2_out), .nLD(in_8), .A(in_7), .CLR(in_2), .B(in_6), .C(in_5), .D(in_4), .Q_A(out_13),
    .Q_B(out_12), .Q_C(out_11), .Q_D(out_10), .CP_U(nand_1_out));
endmodule

module \小型实验室门禁系统  (
  input  in_1,
  input  in_2,
  input  in_3,
  output out_4,
  output out_5,
  output out_6,
  output out_7,
  output out_8,
  output out_9,
  output out_10,
  output out_11,
  output out_12,
  output out_13,
  output out_14,
  output out_15,
  output out_16,
  output out_17,
  output out_18
);

  wire \二进制转8421码电路_1_h_0 , \二进制转8421码电路_1_h_1 , \二进制转8421码电路_1_h_2 , \二进制转8421码电路_1_h_3 ,
       \二进制转8421码电路_1_l_0 , \二进制转8421码电路_1_l_1 , \二进制转8421码电路_1_l_2 , \二进制转8421码电路_1_l_3 , \报警电路_1_out_10 ,
       \报警电路_1_out_11 , \报警电路_1_out_12 , \报警电路_1_out_13 ;

  \报警电路  \u_报警电路_1  (
    .CP_prime__U(in_1), .in_2(in_2), .CP_prime__D(in_3), .WARN(out_18), .out_10(\报警电路_1_out_10 ),
    .out_11(\报警电路_1_out_11 ), .out_12(\报警电路_1_out_12 ), .out_13(\报警电路_1_out_13 ), .in_4(1'b0), .in_5(1'b0),
    .in_6(1'b0), .in_7(1'b0), .in_8(1'b1));
  \二进制转8421码电路  \u_二进制转8421码电路_1  (
    .Q_D(\报警电路_1_out_10 ), .Q_C(\报警电路_1_out_11 ), .Q_B(\报警电路_1_out_12 ), .Q_A(\报警电路_1_out_13 ),
    .H_3(\二进制转8421码电路_1_h_3 ), .H_2(\二进制转8421码电路_1_h_2 ), .H_1(\二进制转8421码电路_1_h_1 ),
    .H_0(\二进制转8421码电路_1_h_0 ), .L_3(\二进制转8421码电路_1_l_3 ), .L_2(\二进制转8421码电路_1_l_2 ),
    .L_1(\二进制转8421码电路_1_l_1 ), .L_0(\二进制转8421码电路_1_l_0 ));
  \显示电路  \u_显示电路_1  (
    .D(\二进制转8421码电路_1_h_3 ), .C(\二进制转8421码电路_1_h_2 ), .B(\二进制转8421码电路_1_h_1 ), .A(\二进制转8421码电路_1_h_0 ),
    .a_2(out_4), .b_2(out_5), .c_2(out_6), .d_2(out_7), .e(out_8), .f(out_9), .g(out_10));
  \显示电路  \u_显示电路_2  (
    .D(\二进制转8421码电路_1_l_3 ), .C(\二进制转8421码电路_1_l_2 ), .B(\二进制转8421码电路_1_l_1 ), .A(\二进制转8421码电路_1_l_0 ),
    .a_2(out_11), .b_2(out_12), .c_2(out_13), .d_2(out_14), .e(out_15), .f(out_16), .g(out_17));
endmodule

module \小型门禁系统测试电路  (
);

  wire button_1_out, button_2_out, button_3_out, \小型实验室门禁系统_1_out_4 , \小型实验室门禁系统_1_out_5 ,
       \小型实验室门禁系统_1_out_6 , \小型实验室门禁系统_1_out_7 , \小型实验室门禁系统_1_out_8 , \小型实验室门禁系统_1_out_9 ,
       \小型实验室门禁系统_1_out_10 , \小型实验室门禁系统_1_out_11 , \小型实验室门禁系统_1_out_12 , \小型实验室门禁系统_1_out_13 ,
       \小型实验室门禁系统_1_out_14 , \小型实验室门禁系统_1_out_15 , \小型实验室门禁系统_1_out_16 , \小型实验室门禁系统_1_out_17 ,
       \小型实验室门禁系统_1_out_18 ;

  _7_Segment_Display u_7_segment_display_1 (
    .g(\小型实验室门禁系统_1_out_10 ), .f(\小型实验室门禁系统_1_out_9 ), .a(\小型实验室门禁系统_1_out_4 ), .b(\小型实验室门禁系统_1_out_5 ),
    .e(\小型实验室门禁系统_1_out_8 ), .d(\小型实验室门禁系统_1_out_7 ), .c(\小型实验室门禁系统_1_out_6 ), .dp(1'b0));
  \小型实验室门禁系统  \u_小型实验室门禁系统_1  (
    .in_1(button_1_out), .in_2(button_2_out), .in_3(button_3_out), .out_4(\小型实验室门禁系统_1_out_4 ),
    .out_5(\小型实验室门禁系统_1_out_5 ), .out_6(\小型实验室门禁系统_1_out_6 ), .out_7(\小型实验室门禁系统_1_out_7 ),
    .out_8(\小型实验室门禁系统_1_out_8 ), .out_9(\小型实验室门禁系统_1_out_9 ), .out_10(\小型实验室门禁系统_1_out_10 ),
    .out_11(\小型实验室门禁系统_1_out_11 ), .out_12(\小型实验室门禁系统_1_out_12 ), .out_13(\小型实验室门禁系统_1_out_13 ),
    .out_14(\小型实验室门禁系统_1_out_14 ), .out_15(\小型实验室门禁系统_1_out_15 ), .out_16(\小型实验室门禁系统_1_out_16 ),
    .out_17(\小型实验室门禁系统_1_out_17 ), .out_18(\小型实验室门禁系统_1_out_18 ));
  Button button_1 (.out(button_1_out));
  Button button_2 (.out(button_2_out));
  Button button_3 (.out(button_3_out));
  _7_Segment_Display u_7_segment_display_2 (
    .g(\小型实验室门禁系统_1_out_17 ), .f(\小型实验室门禁系统_1_out_16 ), .a(\小型实验室门禁系统_1_out_11 ), .b(\小型实验室门禁系统_1_out_12 ),
    .e(\小型实验室门禁系统_1_out_15 ), .d(\小型实验室门禁系统_1_out_14 ), .c(\小型实验室门禁系统_1_out_13 ), .dp(1'b0));
  // Buzzer buzzer_1: pin names not known; wires that end beside it: \小型实验室门禁系统_1_out_18 
  LED led_1 (.in(\小型实验室门禁系统_1_out_18 ));
endmodule
