// Logisim project lab3.circ as structural Verilog: 17 circuits, main circuit 四位乘法器
module \四位乘法器  (
  input  [3:0] in_1,
  input  [3:0] in_2,
  output [7:0] out_3
);

  wire [7:0] adder_1_out, adder_2_out, adder_3_out, adder_4_out, bit_extender_1_out, multiplexer_1_out,
       multiplexer_2_out, multiplexer_3_out;

  assign bit_extender_1_out = {{4{1'b0}}, in_2};  // Bit_Extender bit_extender_1
  Adder adder_1 (.a({8{1'b0}}), .b(bit_extender_1_out), .out(adder_1_out), .cin(1'b0));  // open: cout
  Multiplexer #(.width(8), .disabled(0), .enable("false")) multiplexer_1 (
    .in0({8{1'b0}}), .in1(adder_1_out), .out(multiplexer_1_out), .sel(in_1[0]));
  Adder adder_2 (
    .a(multiplexer_1_out), .b({bit_extender_1_out[6:0], 1'b0}), .out(adder_2_out), .cin(1'b0));  // open: cout
  Multiplexer #(.width(8), .enable("false")) multiplexer_2 (
    .in0(multiplexer_1_out), .in1(adder_2_out), .out(multiplexer_2_out), .sel(in_1[1]));
  Adder adder_3 (
    .a(multiplexer_2_out), .b({bit_extender_1_out[5:0], 2'b00}), .out(adder_3_out), .cin(1'b0));  // open: cout
  Multiplexer #(.width(8), .enable("false")) multiplexer_3 (
    .in0(multiplexer_2_out), .in1(adder_3_out), .out(multiplexer_3_out), .sel(in_1[2]));
  Adder adder_4 (
    .a(multiplexer_3_out), .b({bit_extender_1_out[4:0], 3'b000}), .out(adder_4_out), .cin(1'b0));  // open: cout
  Multiplexer #(.width(8), .enable("false")) multiplexer_4 (
    .in0(multiplexer_3_out), .in1(adder_4_out), .out(out_3), .sel(in_1[3]));
endmodule

module \四位乘法器测试电路  (
  input  [3:0] in_1,
  input  [3:0] in_2,
  output [7:0] out_3
);

  \四位乘法器  \u_四位乘法器_1  (.in_1(in_1), .in_2(in_2), .out_3(out_3));
endmodule

module \_32X4乘法器  (
  input  [3:0] in_1,
  input  [31:0] in_2,
  output [31:0] out_3,
  output [31:0] out_4
);

  wire [31:0] n64adder_1_ch, n64adder_1_cl, n64adder_2_ch, n64adder_2_cl, n64adder_3_ch, n64adder_3_cl,
       n64adder_4_ch, n64adder_4_cl, n64mux_1_ch, n64mux_1_cl, n64mux_2_ch, n64mux_2_cl, n64mux_3_ch,
       n64mux_3_cl, n64shl2_0_1_out_3, n64shl2_0_1_out_4, n64shl2_0_2_out_3, n64shl2_0_2_out_4,
       n64shl2_0_3_out_3, n64shl2_0_3_out_4;

  _64SHL2_0 u_64shl2_0_1 (.in_1(in_2), .in_2({32{1'b0}}), .out_3(n64shl2_0_1_out_3), .out_4(n64shl2_0_1_out_4));
  _64ADDER u_64adder_1 (
    .in_1(1'b0), .AL({32{1'b0}}), .BL(in_2), .AH({32{1'b0}}), .BH({32{1'b0}}), .CL(n64adder_1_cl),
    .CH(n64adder_1_ch));  // open: out_8
  _64MUX u_64mux_1 (
    ._0(in_1[0]), .BL({32{1'b0}}), .AL(n64adder_1_cl), .BH({32{1'b0}}), .AH(n64adder_1_ch), .CL(n64mux_1_cl),
    .CH(n64mux_1_ch));
  _64ADDER u_64adder_2 (
    .in_1(1'b0), .AL(n64mux_1_cl), .BL(n64shl2_0_1_out_3), .AH(n64mux_1_ch), .BH(n64shl2_0_1_out_4),
    .CL(n64adder_2_cl), .CH(n64adder_2_ch));  // open: out_8
  _64SHL2_0 u_64shl2_0_2 (
    .in_1(n64shl2_0_1_out_3), .in_2(n64shl2_0_1_out_4), .out_3(n64shl2_0_2_out_3), .out_4(n64shl2_0_2_out_4));
  _64MUX u_64mux_2 (
    ._0(in_1[1]), .BL(n64mux_1_cl), .AL(n64adder_2_cl), .BH(n64mux_1_ch), .AH(n64adder_2_ch),
    .CL(n64mux_2_cl), .CH(n64mux_2_ch));
  _64SHL2_0 u_64shl2_0_3 (
    .in_1(n64shl2_0_2_out_3), .in_2(n64shl2_0_2_out_4), .out_3(n64shl2_0_3_out_3), .out_4(n64shl2_0_3_out_4));
  _64ADDER u_64adder_3 (
    .in_1(1'b0), .AL(n64mux_2_cl), .BL(n64shl2_0_2_out_3), .AH(n64mux_2_ch), .BH(n64shl2_0_2_out_4),
    .CL(n64adder_3_cl), .CH(n64adder_3_ch));  // open: out_8
  _64MUX u_64mux_3 (
    ._0(in_1[2]), .BL(n64mux_2_cl), .AL(n64adder_3_cl), .BH(n64mux_2_ch), .AH(n64adder_3_ch),
    .CL(n64mux_3_cl), .CH(n64mux_3_ch));
  _64ADDER u_64adder_4 (
    .in_1(1'b0), .AL(n64mux_3_cl), .BL(n64shl2_0_3_out_3), .AH(n64mux_3_ch), .BH(n64shl2_0_3_out_4),
    .CL(n64adder_4_cl), .CH(n64adder_4_ch));  // open: out_8
  _64MUX u_64mux_4 (
    ._0(in_1[3]), .BL(n64mux_3_cl), .AL(n64adder_4_cl), .BH(n64mux_3_ch), .AH(n64adder_4_ch), .CL(out_3),
    .CH(out_4));
endmodule

module \_32X4乘法器测试电路  (
  input  [3:0] in_1,
  input  [31:0] in_2,
  output [31:0] out_3,
  output [31:0] out_4
);

  // Probe on in_1
  // Probe on in_2
  \_32X4乘法器  \u_32x4乘法器_1  (.in_2(in_2), .out_3(out_3), .out_4(out_4), .in_1(in_1));
  // Probe on out_3
  // Probe on out_4
endmodule

module \_32X32乘法器  (
  input  [31:0] in_1,
  input  [31:0] in_2,
  output [31:0] out_3,
  output [31:0] out_4
);

  wire [31:0] \n32x4乘法器_1_out_3 , \n32x4乘法器_1_out_4 , \n32x4乘法器_2_out_3 , \n32x4乘法器_2_out_4 ,
       \n32x4乘法器_3_out_3 , \n32x4乘法器_3_out_4 , \n32x4乘法器_4_out_3 , \n32x4乘法器_4_out_4 , \n32x4乘法器_5_out_3 ,
       \n32x4乘法器_5_out_4 , \n32x4乘法器_6_out_3 , \n32x4乘法器_6_out_4 , \n32x4乘法器_7_out_3 , \n32x4乘法器_7_out_4 ,
       \n32x4乘法器_8_out_3 , \n32x4乘法器_8_out_4 , n64adder_1_ch, n64adder_1_cl, n64adder_2_ch, n64adder_2_cl,
       n64adder_3_ch, n64adder_3_cl, n64adder_4_ch, n64adder_4_cl, n64adder_5_ch, n64adder_5_cl,
       n64adder_6_ch, n64adder_6_cl, n64shl2_4_1_oh, n64shl2_4_1_ol, n64shl2_8_1_oh, n64shl2_8_1_ol,
       n64shl2_12_1_oh, n64shl2_12_1_ol, n64shl2_16_1_oh, n64shl2_16_1_ol, n64shl2_20_1_oh, n64shl2_20_1_ol,
       n64shl2_24_1_oh, n64shl2_24_1_ol, n64shl2_28_1_oh, n64shl2_28_1_ol;

  \_32X4乘法器  \u_32x4乘法器_1  (.in_2(in_2), .out_3(\n32x4乘法器_1_out_3 ), .out_4(\n32x4乘法器_1_out_4 ), .in_1(in_1[3:0]));
  \_32X4乘法器  \u_32x4乘法器_2  (.in_2(in_2), .out_3(\n32x4乘法器_2_out_3 ), .out_4(\n32x4乘法器_2_out_4 ), .in_1(in_1[7:4]));
  \_32X4乘法器  \u_32x4乘法器_3  (.in_2(in_2), .out_3(\n32x4乘法器_3_out_3 ), .out_4(\n32x4乘法器_3_out_4 ), .in_1(in_1[11:8]));
  \_32X4乘法器  \u_32x4乘法器_4  (.in_2(in_2), .out_3(\n32x4乘法器_4_out_3 ), .out_4(\n32x4乘法器_4_out_4 ), .in_1(in_1[15:12]));
  \_32X4乘法器  \u_32x4乘法器_5  (.in_2(in_2), .out_3(\n32x4乘法器_5_out_3 ), .out_4(\n32x4乘法器_5_out_4 ), .in_1(in_1[19:16]));
  \_32X4乘法器  \u_32x4乘法器_6  (.in_2(in_2), .out_3(\n32x4乘法器_6_out_3 ), .out_4(\n32x4乘法器_6_out_4 ), .in_1(in_1[23:20]));
  \_32X4乘法器  \u_32x4乘法器_7  (.in_2(in_2), .out_3(\n32x4乘法器_7_out_3 ), .out_4(\n32x4乘法器_7_out_4 ), .in_1(in_1[27:24]));
  \_32X4乘法器  \u_32x4乘法器_8  (.in_2(in_2), .out_3(\n32x4乘法器_8_out_3 ), .out_4(\n32x4乘法器_8_out_4 ), .in_1(in_1[31:28]));
  _64SHL2_4 u_64shl2_4_1 (.IL(\n32x4乘法器_2_out_3 ), .IH(\n32x4乘法器_2_out_4 ), .OL(n64shl2_4_1_ol), .OH(n64shl2_4_1_oh));
  _64SHL2_8 u_64shl2_8_1 (.IL(\n32x4乘法器_3_out_3 ), .IH(\n32x4乘法器_3_out_4 ), .OL(n64shl2_8_1_ol), .OH(n64shl2_8_1_oh));
  _64SHL2_12 u_64shl2_12_1 (
    .IL(\n32x4乘法器_4_out_3 ), .IH(\n32x4乘法器_4_out_4 ), .OL(n64shl2_12_1_ol), .OH(n64shl2_12_1_oh));
  _64SHL2_16 u_64shl2_16_1 (
    .IL(\n32x4乘法器_5_out_3 ), .IH(\n32x4乘法器_5_out_4 ), .OL(n64shl2_16_1_ol), .OH(n64shl2_16_1_oh));
  _64SHL2_20 u_64shl2_20_1 (
    .IL(\n32x4乘法器_6_out_3 ), .IH(\n32x4乘法器_6_out_4 ), .OL(n64shl2_20_1_ol), .OH(n64shl2_20_1_oh));
  _64SHL2_24 u_64shl2_24_1 (
    .IL(\n32x4乘法器_7_out_3 ), .IH(\n32x4乘法器_7_out_4 ), .OL(n64shl2_24_1_ol), .OH(n64shl2_24_1_oh));
  _64SHL2_28 u_64shl2_28_1 (
    .IL(\n32x4乘法器_8_out_3 ), .IH(\n32x4乘法器_8_out_4 ), .OL(n64shl2_28_1_ol), .OH(n64shl2_28_1_oh));
  _64ADDER u_64adder_1 (
    .in_1(1'b0), .AL(\n32x4乘法器_1_out_3 ), .BL(n64shl2_4_1_ol), .AH(\n32x4乘法器_1_out_4 ), .BH(n64shl2_4_1_oh),
    .CL(n64adder_1_cl), .CH(n64adder_1_ch));  // open: out_8
  _64ADDER u_64adder_2 (
    .in_1(1'b0), .AL(n64shl2_8_1_ol), .BL(n64shl2_12_1_ol), .AH(n64shl2_8_1_oh), .BH(n64shl2_12_1_oh),
    .CL(n64adder_2_cl), .CH(n64adder_2_ch));  // open: out_8
  _64ADDER u_64adder_3 (
    .in_1(1'b0), .AL(n64shl2_16_1_ol), .BL(n64shl2_20_1_ol), .AH(n64shl2_16_1_oh), .BH(n64shl2_20_1_oh),
    .CL(n64adder_3_cl), .CH(n64adder_3_ch));  // open: out_8
  _64ADDER u_64adder_4 (
    .in_1(1'b0), .AL(n64shl2_24_1_ol), .BL(n64shl2_28_1_ol), .AH(n64shl2_24_1_oh), .BH(n64shl2_28_1_oh),
    .CL(n64adder_4_cl), .CH(n64adder_4_ch));  // open: out_8
  _64ADDER u_64adder_5 (
    .in_1(1'b0), .AL(n64adder_1_cl), .BL(n64adder_2_cl), .AH(n64adder_1_ch), .BH(n64adder_2_ch),
    .CL(n64adder_5_cl), .CH(n64adder_5_ch));  // open: out_8
  _64ADDER u_64adder_6 (
    .in_1(1'b0), .AL(n64adder_3_cl), .BL(n64adder_4_cl), .AH(n64adder_3_ch), .BH(n64adder_4_ch),
    .CL(n64adder_6_cl), .CH(n64adder_6_ch));  // open: out_8
  _64ADDER u_64adder_7 (
    .in_1(1'b0), .AL(n64adder_5_cl), .BL(n64adder_6_cl), .AH(n64adder_5_ch), .BH(n64adder_6_ch), .CL(out_3),
    .CH(out_4));  // open: out_8
endmodule

module \_32X32乘法器测试电路  (
  input  [31:0] in_1,
  input  [31:0] in_2,
  output [31:0] out_3,
  output [31:0] out_4
);

  // Probe on in_1
  // Probe on in_2
  \_32X32乘法器  \u_32x32乘法器_1  (.in_1(in_1), .in_2(in_2), .out_3(out_3), .out_4(out_4));
  // Probe on out_3
  // Probe on out_4
endmodule

module _32SHL (
  input  [31:0] in_1,
  output [31:0] out_2
);


  assign out_2 = {in_1[30:0], 1'b0};
endmodule

module _64ADDER (
  input  in_1,
  input  [31:0] AL,
  input  [31:0] BL,
  input  [31:0] AH,
  input  [31:0] BH,
  output [31:0] CL,
  output [31:0] CH,
  output out_8
);

  wire adder_1_cout;

  Adder #(.width(32)) adder_1 (.a(AL), .b(BL), .out(CL), .cin(in_1), .cout(adder_1_cout));
  Adder #(.width(32)) adder_2 (.a(AH), .b(BH), .out(CH), .cin(adder_1_cout), .cout(out_8));
endmodule

module _64MUX (
  input  _0,
  input  [31:0] BL,
  input  [31:0] AL,
  input  [31:0] BH,
  input  [31:0] AH,
  output [31:0] CL,
  output [31:0] CH
);

  Multiplexer #(.width(32), .enable("false")) multiplexer_1 (.in0(BL), .in1(AL), .out(CL), .sel(_0));
  Multiplexer #(.width(32), .enable("false")) multiplexer_2 (.in0(BH), .in1(AH), .out(CH), .sel(_0));
endmodule

module _64SHL2_4 (
  input  [31:0] IL,
  input  [31:0] IH,
  output [31:0] OL,
  output [31:0] OH
);


  assign OH = {IH[27:0], IL[31:28]};
  assign OL = {IL[27:0], 4'b0000};
endmodule

module _64SHL2_8 (
  input  [31:0] IL,
  input  [31:0] IH,
  output [31:0] OL,
  output [31:0] OH
);


  assign OH = {IH[23:0], IL[31:24]};
  assign OL = {IL[23:0], {8{1'b0}}};
endmodule

module _64SHL2_12 (
  input  [31:0] IL,
  input  [31:0] IH,
  output [31:0] OL,
  output [31:0] OH
);


  assign OH = {IH[19:0], IL[31:20]};
  assign OL = {IL[19:0], {12{1'b0}}};
endmodule

module _64SHL2_16 (
  input  [31:0] IL,
  input  [31:0] IH,
  output [31:0] OL,
  output [31:0] OH
);


  assign OH = {IH[15:0], IL[31:16]};
  assign OL = {IL[15:0], {16{1'b0}}};
endmodule

module _64SHL2_20 (
  input  [31:0] IL,
  input  [31:0] IH,
  output [31:0] OL,
  output [31:0] OH
);


  assign OH = {IH[11:0], IL[31:12]};
  assign OL = {IL[11:0], {20{1'b0}}};
endmodule

module _64SHL2_24 (
  input  [31:0] IL,
  input  [31:0] IH,
  output [31:0] OL,
  output [31:0] OH
);


  assign OH = {IH[7:0], IL[31:8]};
  assign OL = {IL[7:0], {24{1'b0}}};
endmodule

module _64SHL2_28 (
  input  [31:0] IL,
  input  [31:0] IH,
  output [31:0] OL,
  output [31:0] OH
);


  assign OH = {IH[3:0], IL[31:4]};
  assign OL = {IL[3:0], {28{1'b0}}};
endmodule

module _64SHL2_0 (
  input  [31:0] in_1,
  input  [31:0] in_2,
  output [31:0] out_3,
  output [31:0] out_4
);


  assign out_3 = {in_1[30:0], 1'b0};
  assign out_4 = {in_2[30:0], in_1[31]};
endmodule
