// Logisim project lab4.circ as structural Verilog: 7 circuits, main circuit 四位除法器
module \四位除法器  (
  input  [3:0] n2,
  input  [3:0] d,
  output [3:0] quot,
  output [3:0] rem
);

  wire [2:0] divbodyunit_1_out_4, divbodyunit_2_out_4, divbodyunit_3_out_4;
  wire [3:0] divbodyunit_1_out_5, divbodyunit_2_out_5, divbodyunit_3_out_5;

  DivBodyUnit divbodyunit_1 (
    .in_1(n2[2:0]), .in_2({3'b000, n2[3]}), .in_3(d), .out_4(divbodyunit_1_out_4), .out_5(divbodyunit_1_out_5));
  DivBodyUnit divbodyunit_2 (
    .in_1(divbodyunit_1_out_4), .in_2(divbodyunit_1_out_5), .in_3(d), .out_4(divbodyunit_2_out_4),
    .out_5(divbodyunit_2_out_5));
  DivFoot divfoot_1 (.in_1(divbodyunit_3_out_4), .in_2(divbodyunit_3_out_5), .in_3(d), .out_4(quot), .out_5(rem));
  DivBodyUnit divbodyunit_3 (
    .in_1(divbodyunit_2_out_4), .in_2(divbodyunit_2_out_5), .in_3(d), .out_4(divbodyunit_3_out_4),
    .out_5(divbodyunit_3_out_5));
endmodule

module \四位除法器测试电路  (
  input  [3:0] in_1,
  input  [3:0] in_2,
  output [3:0] out_3,
  output [3:0] out_4
);

  // Probe on in_1
  // Probe on in_2
  \四位除法器  \u_四位除法器_1  (.n2(in_1), .d(in_2), .quot(out_3), .rem(out_4));
  // Probe on out_3
  // Probe on out_4
endmodule

module \_32位除法器  (
  input  [31:0] in_1,
  input  [31:0] in_2,
  output [31:0] out_3,
  output [31:0] out_4
);

  wire [31:0] div1_1_out_4, div1_1_out_5, div1_2_out_4, div1_2_out_5, div1_3_out_4, div1_3_out_5,
       div1_4_out_4, div1_4_out_5, div1_5_out_4, div1_5_out_5, div1_6_out_4, div1_6_out_5, div1_7_out_4,
       div1_7_out_5, div1_8_out_4, div1_8_out_5, div1_9_out_4, div1_9_out_5, div1_10_out_4, div1_10_out_5,
       div1_11_out_4, div1_11_out_5, div1_12_out_4, div1_12_out_5, div1_13_out_4, div1_13_out_5,
       div1_14_out_4, div1_14_out_5, div1_15_out_4, div1_15_out_5, div1_16_out_4, div1_16_out_5,
       div1_17_out_4, div1_17_out_5, div1_18_out_4, div1_18_out_5, div1_19_out_4, div1_19_out_5,
       div1_20_out_4, div1_20_out_5, div1_21_out_4, div1_21_out_5, div1_22_out_4, div1_22_out_5,
       div1_23_out_4, div1_23_out_5, div1_24_out_4, div1_24_out_5, div1_25_out_4, div1_25_out_5,
       div1_26_out_4, div1_26_out_5, div1_27_out_4, div1_27_out_5, div1_28_out_4, div1_28_out_5,
       div1_29_out_4, div1_29_out_5, div1_30_out_4, div1_30_out_5, div1_31_out_4, div1_31_out_5;

  Div1 div1_1 (.in_1(in_1), .in_3(in_2), .out_4(div1_1_out_4), .out_5(div1_1_out_5), .in_2({32{1'b0}}));
  Div1 div1_2 (.in_1(div1_29_out_4), .in_3(in_2), .out_4(div1_2_out_4), .out_5(div1_2_out_5), .in_2(div1_29_out_5));
  Div1 div1_3 (.in_1(div1_30_out_4), .in_3(in_2), .out_4(div1_3_out_4), .out_5(div1_3_out_5), .in_2(div1_30_out_5));
  Div1 div1_4 (.in_1(div1_31_out_4), .in_3(in_2), .out_4(div1_4_out_4), .out_5(div1_4_out_5), .in_2(div1_31_out_5));
  Div1 div1_5 (.in_1(div1_1_out_4), .in_3(in_2), .out_4(div1_5_out_4), .out_5(div1_5_out_5), .in_2(div1_1_out_5));
  Div1 div1_6 (.in_1(div1_2_out_4), .in_3(in_2), .out_4(div1_6_out_4), .out_5(div1_6_out_5), .in_2(div1_2_out_5));
  Div1 div1_7 (.in_1(div1_3_out_4), .in_3(in_2), .out_4(div1_7_out_4), .out_5(div1_7_out_5), .in_2(div1_3_out_5));
  Div1 div1_8 (.in_1(div1_4_out_4), .in_3(in_2), .out_4(div1_8_out_4), .out_5(div1_8_out_5), .in_2(div1_4_out_5));
  Div1 div1_9 (.in_1(div1_5_out_4), .in_3(in_2), .out_4(div1_9_out_4), .out_5(div1_9_out_5), .in_2(div1_5_out_5));
  Div1 div1_10 (.in_1(div1_6_out_4), .in_3(in_2), .out_4(div1_10_out_4), .out_5(div1_10_out_5), .in_2(div1_6_out_5));
  Div1 div1_11 (.in_1(div1_7_out_4), .in_3(in_2), .out_4(div1_11_out_4), .out_5(div1_11_out_5), .in_2(div1_7_out_5));
  Div1 div1_12 (.in_1(div1_8_out_4), .in_3(in_2), .out_4(div1_12_out_4), .out_5(div1_12_out_5), .in_2(div1_8_out_5));
  Div1 div1_13 (.in_1(div1_14_out_4), .in_3(in_2), .out_4(div1_13_out_4), .out_5(div1_13_out_5), .in_2(div1_14_out_5));
  Div1 div1_14 (.in_1(div1_9_out_4), .in_3(in_2), .out_4(div1_14_out_4), .out_5(div1_14_out_5), .in_2(div1_9_out_5));
  Div1 div1_15 (.in_1(div1_16_out_4), .in_3(in_2), .out_4(div1_15_out_4), .out_5(div1_15_out_5), .in_2(div1_16_out_5));
  Div1 div1_16 (.in_1(div1_10_out_4), .in_3(in_2), .out_4(div1_16_out_4), .out_5(div1_16_out_5), .in_2(div1_10_out_5));
  Div1 div1_17 (.in_1(div1_11_out_4), .in_3(in_2), .out_4(div1_17_out_4), .out_5(div1_17_out_5), .in_2(div1_11_out_5));
  Div1 div1_18 (.in_1(div1_17_out_4), .in_3(in_2), .out_4(div1_18_out_4), .out_5(div1_18_out_5), .in_2(div1_17_out_5));
  Div1 div1_19 (.in_1(div1_20_out_4), .in_3(in_2), .out_4(div1_19_out_4), .out_5(div1_19_out_5), .in_2(div1_20_out_5));
  Div1 div1_20 (.in_1(div1_12_out_4), .in_3(in_2), .out_4(div1_20_out_4), .out_5(div1_20_out_5), .in_2(div1_12_out_5));
  Div1 div1_21 (.in_1(div1_13_out_4), .in_3(in_2), .out_4(div1_21_out_4), .out_5(div1_21_out_5), .in_2(div1_13_out_5));
  Div1 div1_22 (.in_1(div1_15_out_4), .in_3(in_2), .out_4(div1_22_out_4), .out_5(div1_22_out_5), .in_2(div1_15_out_5));
  Div1 div1_23 (.in_1(div1_18_out_4), .in_3(in_2), .out_4(div1_23_out_4), .out_5(div1_23_out_5), .in_2(div1_18_out_5));
  Div1 div1_24 (.in_1(div1_19_out_4), .in_3(in_2), .out_4(div1_24_out_4), .out_5(div1_24_out_5), .in_2(div1_19_out_5));
  Div1 div1_25 (.in_1(div1_21_out_4), .in_3(in_2), .out_4(div1_25_out_4), .out_5(div1_25_out_5), .in_2(div1_21_out_5));
  Div1 div1_26 (.in_1(div1_22_out_4), .in_3(in_2), .out_4(div1_26_out_4), .out_5(div1_26_out_5), .in_2(div1_22_out_5));
  Div1 div1_27 (.in_1(div1_23_out_4), .in_3(in_2), .out_4(div1_27_out_4), .out_5(div1_27_out_5), .in_2(div1_23_out_5));
  Div1 div1_28 (.in_1(div1_24_out_4), .in_3(in_2), .out_4(div1_28_out_4), .out_5(div1_28_out_5), .in_2(div1_24_out_5));
  Div1 div1_29 (.in_1(div1_25_out_4), .in_3(in_2), .out_4(div1_29_out_4), .out_5(div1_29_out_5), .in_2(div1_25_out_5));
  Div1 div1_30 (.in_1(div1_26_out_4), .in_3(in_2), .out_4(div1_30_out_4), .out_5(div1_30_out_5), .in_2(div1_26_out_5));
  Div1 div1_31 (.in_1(div1_27_out_4), .in_3(in_2), .out_4(div1_31_out_4), .out_5(div1_31_out_5), .in_2(div1_27_out_5));
  Div1 div1_32 (.in_1(div1_28_out_4), .in_3(in_2), .out_4(out_3), .out_5(out_4), .in_2(div1_28_out_5));
endmodule

module \_32位除法器测试电路  (
  input  [31:0] in_1,
  input  [31:0] in_2,
  output [31:0] out_3,
  output [31:0] out_4
);

  // Probe on in_1
  // Probe on in_2
  // Probe on out_3
  \_32位除法器  \u_32位除法器_1  (.in_1(in_1), .in_2(in_2), .out_3(out_3), .out_4(out_4));
  // Probe on out_4
endmodule

module DivBodyUnit (
  input  [2:0] in_1,
  input  [3:0] in_2,
  input  [3:0] in_3,
  output [2:0] out_4,
  output [3:0] out_5
);

  wire comparator_1_lt;
  wire [3:0] subtractor_1_out;
  wire [3:3] multiplexer_1_out;

  Subtractor #(.width(4)) subtractor_1 (.a(in_2), .b(in_3), .out(subtractor_1_out), .bin(1'b0));  // open: bout
  Comparator #(.width(4), .mode("unsigned")) comparator_1 (.a(in_2), .b(in_3), .lt(comparator_1_lt));  // open: gt, eq
  Multiplexer #(.width(4), .enable("false")) multiplexer_1 (
    .in0(in_2), .in1(subtractor_1_out), .out({multiplexer_1_out[3], out_5[3:1]}), .sel(out_4[0]));
  not not_1 (out_4[0], comparator_1_lt);

  assign out_4[2:1] = in_1[1:0];
  assign out_5[0] = in_1[2];
endmodule

module DivFoot (
  input  [2:0] in_1,
  input  [3:0] in_2,
  input  [3:0] in_3,
  output [3:0] out_4,
  output [3:0] out_5
);

  wire comparator_1_lt;
  wire [3:0] subtractor_1_out;

  Subtractor #(.width(4)) subtractor_1 (.a(in_2), .b(in_3), .out(subtractor_1_out), .bin(1'b0));  // open: bout
  Comparator #(.width(4), .mode("unsigned")) comparator_1 (.a(in_2), .b(in_3), .lt(comparator_1_lt));  // open: gt, eq
  Multiplexer #(.width(4), .enable("false")) multiplexer_1 (
    .in0(in_2), .in1(subtractor_1_out), .out(out_5), .sel(out_4[0]));
  not not_1 (out_4[0], comparator_1_lt);

  assign out_4[3:1] = in_1;
endmodule

module Div1 (
  input  [31:0] in_1,
  input  [31:0] in_2,
  input  [31:0] in_3,
  output [31:0] out_4,
  output [31:0] out_5
);

  wire comparator_1_lt;
  wire [31:0] subtractor_1_out;

  Subtractor #(.width(32)) subtractor_1 (
    .a({in_2[30:0], in_1[31]}), .b(in_3), .out(subtractor_1_out), .bin(1'b0));  // open: bout
  Comparator #(.width(32), .mode("unsigned")) comparator_1 (
    .a({in_2[30:0], in_1[31]}), .b(in_3), .lt(comparator_1_lt));  // open: gt, eq
  not not_1 (out_4[0], comparator_1_lt);
  Multiplexer #(.width(32), .enable("false")) multiplexer_1 (
    .in0({in_2[30:0], in_1[31]}), .in1(subtractor_1_out), .out(out_5), .sel(out_4[0]));

  assign out_4[31:1] = in_1[30:0];
endmodule
