// Logisim project lab5.circ as structural Verilog: 23 circuits, main circuit 多功能数字钟
module \四位二进制可逆计数器  (
  input  CP_U,
  input  CP_D,
  input  nLD,
  input  A,
  input  CLR,
  input  B,
  input  C,
  input  D,
  output Q_A,
  output Q_B,
  output Q_C,
  output Q_D
);

  wire and_1_out, and_2_out, and_3_out, and_4_out, and_5_out, and_6_out, and_7_out, and_8_out, and_9_out,
       and_10_out, and_11_out, and_12_out, and_13_out, and_14_out, d_ff_1_qn, d_ff_2_qn, d_ff_3_qn,
       d_ff_4_qn, not_1_out, not_2_out, not_3_out, or_1_out, or_2_out, or_3_out, or_4_out, or_5_out,
       or_6_out, or_7_out, or_8_out;

  not not_1 (not_1_out, CP_U);
  not not_2 (not_2_out, CP_D);
  not not_3 (not_3_out, nLD);
  or or_1 (or_1_out, not_1_out, not_2_out);
  and and_1 (and_1_out, not_3_out, ~CLR, A);  // AND_Gate
  and and_2 (and_2_out, Q_A, not_1_out);
  and and_3 (and_3_out, d_ff_1_qn, not_2_out);
  and and_4 (and_4_out, not_3_out, ~CLR, B);  // AND_Gate
  and and_5 (and_5_out, Q_A, Q_B, not_1_out);
  and and_6 (and_6_out, d_ff_1_qn, d_ff_2_qn, not_2_out);
  and and_7 (and_7_out, not_3_out, ~CLR, C);  // AND_Gate
  and and_8 (and_8_out, Q_A, Q_B, Q_C, not_1_out);
  and and_9 (and_9_out, d_ff_1_qn, d_ff_2_qn, d_ff_3_qn, not_2_out);
  and and_10 (and_10_out, not_3_out, ~CLR, D);  // AND_Gate
  and and_11 (and_11_out, not_3_out, ~and_1_out);  // AND_Gate
  or or_2 (or_2_out, and_2_out, and_3_out);
  and and_12 (and_12_out, not_3_out, ~and_4_out);  // AND_Gate
  or or_3 (or_3_out, and_5_out, and_6_out);
  and and_13 (and_13_out, not_3_out, ~and_7_out);  // AND_Gate
  or or_4 (or_4_out, and_8_out, and_9_out);
  and and_14 (and_14_out, not_3_out, ~and_10_out);  // AND_Gate
  D_Flip_Flop #(.trigger("falling")) d_ff_1 (
    .clk(or_1_out), .D(d_ff_1_qn), .Q(Q_A), .Qn(d_ff_1_qn), .preset(and_1_out), .reset(or_5_out));
  or or_5 (or_5_out, and_11_out, CLR);
  D_Flip_Flop #(.trigger("falling")) d_ff_2 (
    .clk(or_2_out), .D(d_ff_2_qn), .Q(Q_B), .Qn(d_ff_2_qn), .preset(and_4_out), .reset(or_6_out));
  or or_6 (or_6_out, and_12_out, CLR);
  D_Flip_Flop #(.trigger("falling")) d_ff_3 (
    .clk(or_3_out), .D(d_ff_3_qn), .Q(Q_C), .Qn(d_ff_3_qn), .preset(and_7_out), .reset(or_7_out));
  or or_7 (or_7_out, and_13_out, CLR);
  D_Flip_Flop #(.trigger("falling")) d_ff_4 (
    .clk(or_4_out), .D(d_ff_4_qn), .Q(Q_D), .Qn(d_ff_4_qn), .preset(and_10_out), .reset(or_8_out));
  or or_8 (or_8_out, and_14_out, CLR);
endmodule

module \六十进制计数器  (
  input  Clr,
  input  Adj,
  input  Cpu,
  input  Cpd,
  output Q0d,
  output Q0c,
  output Q0b,
  output Q0a,
  output Q1d,
  output Q1c,
  output Q1b,
  output Q1a,
  output nQcc
);

  wire and_1_out, and_2_out, and_3_out, and_4_out, nand_1_out, nor_1_out, not_1_out, not_2_out, not_3_out,
       not_4_out, or_1_out, or_2_out, or_3_out, or_4_out, or_5_out, or_6_out;
  wire [3:0] multiplexer_1_out, multiplexer_2_out;

  nand nand_1 (nand_1_out, Adj, Cpd);
  not not_1 (not_1_out, Cpu);
  or or_1 (or_1_out, and_1_out, Clr);
  or or_2 (or_2_out, nand_1_out, nor_1_out);
  nor nor_1 (nor_1_out, or_6_out, or_3_out);
  Multiplexer #(.width(4), .enable("false")) multiplexer_1 (
    .in0(4'b0000), .in1(4'b1001), .out(multiplexer_1_out), .sel(and_2_out));
  or or_3 (or_3_out, Q0d, Q0c, Q0b, Q0a);
  \四位二进制可逆计数器  L (
    .CP_D(or_2_out), .nLD(not_2_out), .A(multiplexer_1_out[0]), .CLR(or_1_out), .B(multiplexer_1_out[1]),
    .C(multiplexer_1_out[2]), .D(multiplexer_1_out[3]), .Q_A(Q0a), .Q_B(Q0b), .Q_C(Q0c), .Q_D(Q0d),
    .CP_U(not_1_out));
  not not_2 (not_2_out, and_2_out);
  and and_1 (and_1_out, Q0d, ~Q0c, Q0b, ~Q0a);  // AND_Gate
  and and_2 (and_2_out, Q0d, Q0c, Q0b, Q0a);
  not not_3 (not_3_out, and_1_out);
  or or_4 (or_4_out, and_3_out, Clr);
  or or_5 (or_5_out, ~or_6_out, ~and_2_out);  // OR_Gate
  or or_6 (or_6_out, Q1d, Q1c, Q1b, Q1a);
  Multiplexer #(.width(4), .enable("false")) multiplexer_2 (
    .in0(4'b0000), .in1(4'b0101), .out(multiplexer_2_out), .sel(and_4_out));
  \四位二进制可逆计数器  H (
    .CP_D(or_5_out), .nLD(not_4_out), .A(multiplexer_2_out[0]), .CLR(or_4_out), .B(multiplexer_2_out[1]),
    .C(multiplexer_2_out[2]), .D(multiplexer_2_out[3]), .Q_A(Q1a), .Q_B(Q1b), .Q_C(Q1c), .Q_D(Q1d),
    .CP_U(not_3_out));
  and and_3 (and_3_out, ~Q1d, Q1c, Q1b, ~Q1a);  // AND_Gate
  and and_4 (and_4_out, Q1d, Q1c, Q1b, Q1a);
  not not_4 (not_4_out, and_4_out);
  and and_5 (nQcc, and_3_out, ~Adj);  // AND_Gate
endmodule

module \六十进制计数器测试电路  (
  input  in_1,
  input  in_2,
  output out_3
);

  wire button_1_out, button_2_out, d_ff_1_qn, \六十进制计数器_1_q0a , \六十进制计数器_1_q0b , \六十进制计数器_1_q0c ,
       \六十进制计数器_1_q0d , \六十进制计数器_1_q1a , \六十进制计数器_1_q1b , \六十进制计数器_1_q1c , \六十进制计数器_1_q1d ;
  wire [3:0] led_base_1_out_5, led_base_2_out_5;

  Button button_1 (.out(button_1_out));
  Button button_2 (.out(button_2_out));
  Hex_Digit_Display hex_digit_display_1 (.value(led_base_1_out_5), .dp(1'b0));
  led_base led_base_1 (
    .in_1(\六十进制计数器_1_q1a ), .in_2(\六十进制计数器_1_q1b ), .in_3(\六十进制计数器_1_q1c ), .in_4(\六十进制计数器_1_q1d ),
    .out_5(led_base_1_out_5));
  Hex_Digit_Display hex_digit_display_2 (.value(led_base_2_out_5), .dp(1'b0));
  led_base led_base_2 (
    .in_1(\六十进制计数器_1_q0a ), .in_2(\六十进制计数器_1_q0b ), .in_3(\六十进制计数器_1_q0c ), .in_4(\六十进制计数器_1_q0d ),
    .out_5(led_base_2_out_5));
  \六十进制计数器  \u_六十进制计数器_1  (
    .Clr(in_2), .Adj(in_1), .Cpu(button_1_out), .Cpd(button_2_out), .nQcc(out_3), .Q0d(\六十进制计数器_1_q0d ),
    .Q0c(\六十进制计数器_1_q0c ), .Q0b(\六十进制计数器_1_q0b ), .Q0a(\六十进制计数器_1_q0a ), .Q1d(\六十进制计数器_1_q1d ),
    .Q1c(\六十进制计数器_1_q1c ), .Q1b(\六十进制计数器_1_q1b ), .Q1a(\六十进制计数器_1_q1a ));
  D_Flip_Flop d_ff_1 (.clk(out_3), .D(d_ff_1_qn), .Qn(d_ff_1_qn));  // open: Q, preset, reset
endmodule

module \十二进制计数器或二十四进制的计数器  (
  input  Set,
  input  Clr,
  input  Cpu,
  input  Adj,
  input  Cpd,
  output Q1d,
  output Q1c,
  output Q1b,
  output Q1a,
  output nQcc,
  output Q0d,
  output Q0c,
  output Q0b,
  output Q0a
);

  wire and_1_out, mini_d_ff_1_out_3, multiplexer_1_out, n0_11_counter_1_out_7, n0_11_counter_1_qcc;
  wire [3:0] n0_11_counter_1_i;
  wire [4:0] adder_1_out, and_2_out, n1to5_1_out_2, n1to5_2_out_2, n4to5_1_out_2;

  // Probe on n0_11_counter_1_i
  _1to5 u_1to5_1 (.in_1(Set), .out_2(n1to5_1_out_2));
  _1to5 u_1to5_2 (.in_1(n0_11_counter_1_qcc), .out_2(n1to5_2_out_2));
  _0_11_counter u_0_11_counter_1 (
    .Clr(Clr), .Adj(Adj), .Cpu(Cpu), .Cpd(Cpd), .i(n0_11_counter_1_i), .rst_d(and_1_out),
    .Qcc(n0_11_counter_1_qcc), .out_7(n0_11_counter_1_out_7));
  and and_1 (and_1_out, n0_11_counter_1_qcc, n0_11_counter_1_out_7, Cpd);
  _4to5 u_4to5_1 (.in_1(n0_11_counter_1_i), .out_2(n4to5_1_out_2));
  assign and_2_out = 5'b01100 & n1to5_1_out_2 & n1to5_2_out_2;  // AND_Gate and_2, 5 bits wide
  Multiplexer #(.enable("false")) multiplexer_1 (
    .in0(n0_11_counter_1_qcc), .in1(mini_d_ff_1_out_3), .out(multiplexer_1_out), .sel(Set));
  mini_d_ff mini_d_ff_1 (.in_1(n0_11_counter_1_qcc), .out_3(mini_d_ff_1_out_3), .in_2(Clr));
  Adder #(.width(5)) adder_1 (.a(n4to5_1_out_2), .b(and_2_out), .out(adder_1_out), .cin(1'b0));  // open: cout
  not not_1 (nQcc, multiplexer_1_out);
  // Probe on adder_1_out
  _5bits2BCD u_5bits2bcd_1 (
    .e(adder_1_out[4]), .h3(Q1d), .d(adder_1_out[3]), .h2(Q1c), .c(adder_1_out[2]), .h1(Q1b),
    .b(adder_1_out[1]), .a(adder_1_out[0]), .h0(Q1a), .b3(Q0d), .b2(Q0c), .b1(Q0b), .b0(Q0a));
endmodule

module \十二进制计数器或二十四进制的计数器测试电路  (
  input  in_1,
  output out_2
);

  wire button_1_out, button_2_out, d_ff_1_qn, \十二进制计数器或二十四进制的计数器_1_q0a , \十二进制计数器或二十四进制的计数器_1_q0b ,
       \十二进制计数器或二十四进制的计数器_1_q0c , \十二进制计数器或二十四进制的计数器_1_q0d , \十二进制计数器或二十四进制的计数器_1_q1a ,
       \十二进制计数器或二十四进制的计数器_1_q1b , \十二进制计数器或二十四进制的计数器_1_q1c , \十二进制计数器或二十四进制的计数器_1_q1d ;
  wire [3:0] led_base_1_out_5, led_base_2_out_5;

  Button button_1 (.out(button_1_out));
  Button button_2 (.out(button_2_out));
  Hex_Digit_Display hex_digit_display_1 (.value(led_base_1_out_5), .dp(1'b0));
  led_base led_base_1 (
    .in_1(\十二进制计数器或二十四进制的计数器_1_q1a ), .in_2(\十二进制计数器或二十四进制的计数器_1_q1b ), .in_3(\十二进制计数器或二十四进制的计数器_1_q1c ),
    .in_4(\十二进制计数器或二十四进制的计数器_1_q1d ), .out_5(led_base_1_out_5));
  Hex_Digit_Display hex_digit_display_2 (.value(led_base_2_out_5), .dp(1'b0));
  led_base led_base_2 (
    .in_1(\十二进制计数器或二十四进制的计数器_1_q0a ), .in_2(\十二进制计数器或二十四进制的计数器_1_q0b ), .in_3(\十二进制计数器或二十四进制的计数器_1_q0c ),
    .in_4(\十二进制计数器或二十四进制的计数器_1_q0d ), .out_5(led_base_2_out_5));
  \十二进制计数器或二十四进制的计数器  \u_十二进制计数器或二十四进制的计数器_1  (
    .Set(in_1), .Clr(1'b0), .Cpu(button_1_out), .Adj(1'b1), .Cpd(button_2_out),
    .Q1d(\十二进制计数器或二十四进制的计数器_1_q1d ), .Q1c(\十二进制计数器或二十四进制的计数器_1_q1c ), .Q1b(\十二进制计数器或二十四进制的计数器_1_q1b ),
    .Q1a(\十二进制计数器或二十四进制的计数器_1_q1a ), .nQcc(out_2), .Q0d(\十二进制计数器或二十四进制的计数器_1_q0d ),
    .Q0c(\十二进制计数器或二十四进制的计数器_1_q0c ), .Q0b(\十二进制计数器或二十四进制的计数器_1_q0b ), .Q0a(\十二进制计数器或二十四进制的计数器_1_q0a ));
  D_Flip_Flop d_ff_1 (.clk(out_2), .D(d_ff_1_qn), .Qn(d_ff_1_qn));  // open: Q, preset, reset
endmodule

module \上下午文字显示  (
  input  AMPM,
  input  TT,
  output [4:0] out_3,
  output [4:0] out_4,
  output [4:0] out_5,
  output [4:0] out_6
);

  wire [4:0] multiplexer_1_out, multiplexer_2_out;

  Multiplexer #(.width(5), .enable("false")) multiplexer_1 (
    .in0(5'b00001), .in1(5'b10000), .out(multiplexer_1_out), .sel(AMPM));
  Multiplexer #(.width(5), .enable("false")) multiplexer_2 (
    .in0(5'b00101), .in1(5'b10100), .out(multiplexer_2_out), .sel(AMPM));
  assign out_3 = multiplexer_1_out & {5{TT}};  // AND_Gate and_1, 5 bits wide
  assign out_4 = {5{1'b1}} & {5{TT}};  // AND_Gate and_2, 5 bits wide
  assign out_5 = multiplexer_2_out & {5{TT}};  // AND_Gate and_3, 5 bits wide

  assign out_6 = out_3;
endmodule

module \上下午文字显示测试电路  (
  input  in_1,
  input  in_2
);

  wire [4:0] \上下午文字显示_1_out_3 , \上下午文字显示_1_out_4 , \上下午文字显示_1_out_5 , \上下午文字显示_1_out_6 ;

  DotMatrix #(.matrixcols(4), .matrixrows(5)) dotmatrix_1 (
    .col0(\上下午文字显示_1_out_3 ), .col1(\上下午文字显示_1_out_4 ), .col2(\上下午文字显示_1_out_5 ), .col3(\上下午文字显示_1_out_6 ));
  \上下午文字显示  \u_上下午文字显示_1  (
    .AMPM(in_1), .TT(in_2), .out_3(\上下午文字显示_1_out_3 ), .out_4(\上下午文字显示_1_out_4 ), .out_5(\上下午文字显示_1_out_5 ),
    .out_6(\上下午文字显示_1_out_6 ));
endmodule

module \电子钟整点报时  (
  input  [3:0] MH,
  input  [3:0] SH,
  input  [3:0] ML,
  output out_4
);

  wire and_1_out, and_3_out;

  and and_1 (and_1_out, ~MH[3], MH[2], ~MH[1], MH[0], ML[3], ~ML[2], ~ML[1], ML[0]);  // AND_Gate
  and and_2 (out_4, and_1_out, and_3_out);
  and and_3 (and_3_out, ~SH[3], SH[2], ~SH[1], SH[0]);  // AND_Gate
endmodule

module \秒脉冲产生电路  (
  input  in_1,
  output out_2
);

  wire d_ff_1_q, d_ff_1_qn, d_ff_2_qn;

  D_Flip_Flop #(.trigger("falling")) d_ff_1 (
    .clk(in_1), .D(d_ff_1_qn), .Q(d_ff_1_q), .Qn(d_ff_1_qn));  // open: preset, reset
  D_Flip_Flop #(.trigger("falling")) d_ff_2 (
    .clk(d_ff_1_q), .D(d_ff_2_qn), .Q(out_2), .Qn(d_ff_2_qn));  // open: preset, reset
endmodule

module \多功能数字钟  (
  input  CPu,
  input  CPd,
  input  Set,
  input  Clr,
  input  Adj0,
  input  CP,
  input  Adj1,
  output [4:0] out_8,
  output alarm,
  output [4:0] out_10,
  output [4:0] out_11,
  output [4:0] out_12,
  output teller,
  output [3:0] out_14,
  output [3:0] out_15,
  output [3:0] out_16,
  output [3:0] out_17,
  output [3:0] out_18,
  output [3:0] out_19
);

  wire and_1_out, and_2_out, and_3_out, and_4_out, and_5_out, and_6_out, not_1_out, not_2_out, not_3_out,
       or_1_out, or_2_out, or_3_out, \六十进制计数器_1_nqcc , \六十进制计数器_1_q0a , \六十进制计数器_1_q0b , \六十进制计数器_1_q0c ,
       \六十进制计数器_1_q0d , \六十进制计数器_1_q1a , \六十进制计数器_1_q1b , \六十进制计数器_1_q1c , \六十进制计数器_1_q1d , \六十进制计数器_2_nqcc ,
       \六十进制计数器_2_q0a , \六十进制计数器_2_q0b , \六十进制计数器_2_q0c , \六十进制计数器_2_q0d , \六十进制计数器_2_q1a , \六十进制计数器_2_q1b ,
       \六十进制计数器_2_q1c , \六十进制计数器_2_q1d , \十二进制计数器或二十四进制的计数器_1_nqcc , \十二进制计数器或二十四进制的计数器_1_q0a ,
       \十二进制计数器或二十四进制的计数器_1_q0b , \十二进制计数器或二十四进制的计数器_1_q0c , \十二进制计数器或二十四进制的计数器_1_q0d ,
       \十二进制计数器或二十四进制的计数器_1_q1a , \十二进制计数器或二十四进制的计数器_1_q1b , \十二进制计数器或二十四进制的计数器_1_q1c ,
       \十二进制计数器或二十四进制的计数器_1_q1d , \秒脉冲产生电路_1_out_2 ;

  not not_1 (not_1_out, Set);
  and and_1 (and_1_out, Adj0, ~Adj1);  // AND_Gate
  or or_1 (or_1_out, Adj0, Adj1);
  and and_2 (and_2_out, and_1_out, CPu);
  and and_3 (and_3_out, ~or_1_out, \六十进制计数器_1_nqcc );  // AND_Gate
  \上下午文字显示  \u_上下午文字显示_1  (
    .AMPM(not_2_out), .TT(not_1_out), .out_3(out_8), .out_4(out_10), .out_5(out_11), .out_6(out_12));
  not not_2 (not_2_out, \十二进制计数器或二十四进制的计数器_1_nqcc );
  or or_2 (or_2_out, and_3_out, and_2_out);
  hour_fix hour_fix_1 (
    .L(out_15), .H(out_14), .H3(\十二进制计数器或二十四进制的计数器_1_q1d ), .H2(\十二进制计数器或二十四进制的计数器_1_q1c ),
    .H1(\十二进制计数器或二十四进制的计数器_1_q1b ), .H0(\十二进制计数器或二十四进制的计数器_1_q1a ), .L3(\十二进制计数器或二十四进制的计数器_1_q0d ),
    .L2(\十二进制计数器或二十四进制的计数器_1_q0c ), .L1(\十二进制计数器或二十四进制的计数器_1_q0b ), .L0(\十二进制计数器或二十四进制的计数器_1_q0a ),
    .nSet(not_1_out));
  and and_4 (and_4_out, Adj0, Adj1);
  \十二进制计数器或二十四进制的计数器  \u_十二进制计数器或二十四进制的计数器_1  (
    .Set(Set), .Clr(Clr), .Cpu(or_2_out), .Adj(and_1_out), .Cpd(CPd), .Q1d(\十二进制计数器或二十四进制的计数器_1_q1d ),
    .Q1c(\十二进制计数器或二十四进制的计数器_1_q1c ), .Q1b(\十二进制计数器或二十四进制的计数器_1_q1b ), .Q1a(\十二进制计数器或二十四进制的计数器_1_q1a ),
    .nQcc(\十二进制计数器或二十四进制的计数器_1_nqcc ), .Q0d(\十二进制计数器或二十四进制的计数器_1_q0d ), .Q0c(\十二进制计数器或二十四进制的计数器_1_q0c ),
    .Q0b(\十二进制计数器或二十四进制的计数器_1_q0b ), .Q0a(\十二进制计数器或二十四进制的计数器_1_q0a ));
  and and_5 (and_5_out, ~or_1_out, \六十进制计数器_2_nqcc );  // AND_Gate
  and and_6 (and_6_out, CPu, and_4_out);
  not not_3 (not_3_out, \十二进制计数器或二十四进制的计数器_1_nqcc );
  or or_3 (or_3_out, and_5_out, and_6_out);
  led_base led_base_1 (
    .in_1(\六十进制计数器_1_q1a ), .in_2(\六十进制计数器_1_q1b ), .in_3(\六十进制计数器_1_q1c ), .in_4(\六十进制计数器_1_q1d ),
    .out_5(out_16));
  led_base led_base_2 (
    .in_1(\六十进制计数器_1_q0a ), .in_2(\六十进制计数器_1_q0b ), .in_3(\六十进制计数器_1_q0c ), .in_4(\六十进制计数器_1_q0d ),
    .out_5(out_17));
  \六十进制计数器  \u_六十进制计数器_1  (
    .Clr(Clr), .Adj(and_4_out), .Cpu(or_3_out), .Cpd(CPd), .nQcc(\六十进制计数器_1_nqcc ), .Q0d(\六十进制计数器_1_q0d ),
    .Q0c(\六十进制计数器_1_q0c ), .Q0b(\六十进制计数器_1_q0b ), .Q0a(\六十进制计数器_1_q0a ), .Q1d(\六十进制计数器_1_q1d ),
    .Q1c(\六十进制计数器_1_q1c ), .Q1b(\六十进制计数器_1_q1b ), .Q1a(\六十进制计数器_1_q1a ));
  \秒脉冲产生电路  \u_秒脉冲产生电路_1  (.out_2(\秒脉冲产生电路_1_out_2 ), .in_1(CP));
  \电子钟整点报时  \u_电子钟整点报时_1  (.out_4(teller), .MH(out_16), .ML(out_17), .SH(out_18));
  led_base led_base_3 (
    .in_1(\六十进制计数器_2_q1a ), .in_2(\六十进制计数器_2_q1b ), .in_3(\六十进制计数器_2_q1c ), .in_4(\六十进制计数器_2_q1d ),
    .out_5(out_18));
  led_base led_base_4 (
    .in_1(\六十进制计数器_2_q0a ), .in_2(\六十进制计数器_2_q0b ), .in_3(\六十进制计数器_2_q0c ), .in_4(\六十进制计数器_2_q0d ),
    .out_5(out_19));
  \闹钟  \u_闹钟_1  (
    .SH(out_18), .HH(out_14), .SL(out_19), .HH_(4'b0000), .HL(out_15), .HL_(4'b1000), .MH(out_16),
    .MH_(4'b0000), .ML(out_17), .ML_(4'b0000), .out_14(alarm), .isPM(not_3_out), .isPM_(1'b1), .en(1'b1));
  \六十进制计数器  \u_六十进制计数器_2  (
    .Clr(Clr), .Adj(1'b0), .Cpu(\秒脉冲产生电路_1_out_2 ), .Cpd(1'b0), .nQcc(\六十进制计数器_2_nqcc ),
    .Q0d(\六十进制计数器_2_q0d ), .Q0c(\六十进制计数器_2_q0c ), .Q0b(\六十进制计数器_2_q0b ), .Q0a(\六十进制计数器_2_q0a ),
    .Q1d(\六十进制计数器_2_q1d ), .Q1c(\六十进制计数器_2_q1c ), .Q1b(\六十进制计数器_2_q1b ), .Q1a(\六十进制计数器_2_q1a ));
endmodule

module \多功能数字钟测试电路  (
  input  in_1,
  input  in_2,
  input  in_3,
  input  in_4
);

  wire button_1_out, button_2_out, clock_1_out, \多功能数字钟_1_alarm , \多功能数字钟_1_teller ;
  wire [3:0] \多功能数字钟_1_out_14 , \多功能数字钟_1_out_15 , \多功能数字钟_1_out_16 , \多功能数字钟_1_out_17 , \多功能数字钟_1_out_18 ,
       \多功能数字钟_1_out_19 ;
  wire [4:0] \多功能数字钟_1_out_8 , \多功能数字钟_1_out_10 , \多功能数字钟_1_out_11 , \多功能数字钟_1_out_12 ;

  DotMatrix #(.matrixcols(4), .matrixrows(5)) dotmatrix_1 (
    .col0(\多功能数字钟_1_out_8 ), .col1(\多功能数字钟_1_out_10 ), .col2(\多功能数字钟_1_out_11 ), .col3(\多功能数字钟_1_out_12 ));
  Hex_Digit_Display hex_digit_display_1 (.value(\多功能数字钟_1_out_14 ), .dp(1'b0));
  Hex_Digit_Display hex_digit_display_2 (.value(\多功能数字钟_1_out_15 ), .dp(1'b0));
  Clock clock_1 (.out(clock_1_out));
  Button button_1 (.out(button_1_out));
  Hex_Digit_Display hex_digit_display_3 (.value(\多功能数字钟_1_out_16 ), .dp(1'b0));
  Button button_2 (.out(button_2_out));
  Hex_Digit_Display hex_digit_display_4 (.value(\多功能数字钟_1_out_18 ), .dp(1'b0));
  Hex_Digit_Display hex_digit_display_5 (.value(\多功能数字钟_1_out_17 ), .dp(1'b0));
  \多功能数字钟  \u_多功能数字钟_1  (
    .Set(in_3), .Clr(in_4), .Adj0(in_1), .Adj1(in_2), .alarm(\多功能数字钟_1_alarm ), .out_8(\多功能数字钟_1_out_8 ),
    .out_10(\多功能数字钟_1_out_10 ), .out_11(\多功能数字钟_1_out_11 ), .out_12(\多功能数字钟_1_out_12 ),
    .out_14(\多功能数字钟_1_out_14 ), .out_15(\多功能数字钟_1_out_15 ), .out_16(\多功能数字钟_1_out_16 ),
    .out_17(\多功能数字钟_1_out_17 ), .out_18(\多功能数字钟_1_out_18 ), .out_19(\多功能数字钟_1_out_19 ),
    .teller(\多功能数字钟_1_teller ), .CPu(button_1_out), .CPd(button_2_out), .CP(clock_1_out));
  LED led_1 (.in(\多功能数字钟_1_alarm ));
  LED led_2 (.in(\多功能数字钟_1_teller ));
  Hex_Digit_Display hex_digit_display_6 (.value(\多功能数字钟_1_out_19 ), .dp(1'b0));
endmodule

module \闹钟  (
  input  [3:0] SH,
  input  [3:0] HH,
  input  [3:0] HH_,
  input  [3:0] SL,
  input  [3:0] HL,
  input  [3:0] HL_,
  input  isPM,
  input  isPM_,
  input  en,
  input  [3:0] MH,
  input  [3:0] MH_,
  input  [3:0] ML,
  input  [3:0] ML_,
  output out_14
);

  wire and_1_out, and_2_out, comparator_1_eq, comparator_2_eq, comparator_3_eq, comparator_4_eq,
       comparator_5_eq, comparator_6_eq, comparator_7_eq, d_ff_1_q, d_ff_1_qn;
  wire [3:0] register_1_q, register_2_q;

  Comparator #(.width(4), .mode("unsigned")) comparator_1 (.a(HH), .b(HH_), .eq(comparator_1_eq));  // open: gt, lt
  Comparator #(.width(4), .mode("unsigned")) comparator_2 (.a(HL), .b(HL_), .eq(comparator_2_eq));  // open: gt, lt
  Comparator #(.width(1), .mode("unsigned")) comparator_3 (.a(isPM), .b(isPM_), .eq(comparator_3_eq));  // open: gt, lt
  Comparator #(.width(4), .mode("unsigned")) comparator_4 (.a(MH), .b(MH_), .eq(comparator_4_eq));  // open: gt, lt
  Comparator #(.width(4), .mode("unsigned")) comparator_5 (.a(ML), .b(ML_), .eq(comparator_5_eq));  // open: gt, lt
  and and_1 (and_1_out, comparator_1_eq, comparator_2_eq, comparator_3_eq, comparator_4_eq, comparator_5_eq);
  Register #(.width(4), .trigger("high"), .Select("low")) register_1 (
    .D(SH), .en(1'b1), .Q(register_1_q), .clk(and_1_out), .clr(and_1_out), .cs(1'b0), .preset(1'b0));
  Register #(.width(4), .Select("low")) register_2 (
    .D(SL), .en(1'b1), .Q(register_2_q), .clk(and_1_out), .clr(1'b0), .cs(1'b0), .preset(1'b0));
  // Probe on register_1_q
  Comparator #(.width(4), .mode("unsigned")) comparator_6 (
    .a(SH), .b(register_1_q), .eq(comparator_6_eq));  // open: gt, lt
  // Probe on register_2_q
  Comparator #(.width(4), .mode("unsigned")) comparator_7 (
    .a(SL), .b(register_2_q), .eq(comparator_7_eq));  // open: gt, lt
  D_Flip_Flop d_ff_1 (.clk(and_1_out), .D(d_ff_1_qn), .Q(d_ff_1_q), .Qn(d_ff_1_qn), .preset(1'b0), .reset(and_2_out));
  and and_2 (and_2_out, ~comparator_6_eq, comparator_7_eq, d_ff_1_q);  // AND_Gate
  and and_3 (out_14, d_ff_1_q, en);
endmodule

module \闹钟测试电路  (
  input  in_1,
  input  [3:0] in_2,
  input  [3:0] in_3,
  input  [3:0] in_4,
  input  [3:0] in_5,
  input  in_6,
  input  in_7,
  input  [3:0] in_8,
  input  [3:0] in_9,
  input  [3:0] in_10,
  input  [3:0] in_11,
  input  [3:0] in_12,
  input  [3:0] in_13
);

  wire \闹钟_1_out_14 ;

  \闹钟  \u_闹钟_1  (
    .SH(in_12), .HH(in_8), .SL(in_13), .HH_(in_2), .HL(in_9), .HL_(in_3), .MH(in_10), .MH_(in_4), .ML(in_11),
    .ML_(in_5), .out_14(\闹钟_1_out_14 ), .isPM(in_7), .isPM_(in_1), .en(in_6));
  LED led_1 (.in(\闹钟_1_out_14 ));
endmodule

module _0_11_counter (
  input  Adj,
  input  rst_d,
  input  Cpu,
  input  Clr,
  input  Cpd,
  output [3:0] i,
  output out_7,
  output Qcc
);

  wire and_1_out, and_2_out, d_ff_1_qn, nand_1_out, not_1_out, not_2_out, or_1_out, or_2_out;
  wire [3:0] multiplexer_1_out;

  nand nand_1 (nand_1_out, Adj, Cpd);
  not not_1 (not_1_out, Cpu);
  or or_1 (or_1_out, and_1_out, Clr);
  nor nor_1 (out_7, i[3], i[2], i[1], i[0]);
  Multiplexer #(.width(4), .enable("false")) multiplexer_1 (
    .in0(4'b0000), .in1(4'b1011), .out(multiplexer_1_out), .sel(and_2_out));
  \四位二进制可逆计数器  L (
    .CP_D(nand_1_out), .nLD(not_2_out), .A(multiplexer_1_out[0]), .CLR(or_1_out), .B(multiplexer_1_out[1]),
    .C(multiplexer_1_out[2]), .D(multiplexer_1_out[3]), .Q_A(i[0]), .Q_B(i[1]), .Q_C(i[2]), .Q_D(i[3]),
    .CP_U(not_1_out));
  // Probe on i
  and and_1 (and_1_out, i[3], i[2], ~i[1], ~i[0]);  // AND_Gate
  and and_2 (and_2_out, i[3], i[2], i[1], i[0]);
  not not_2 (not_2_out, and_2_out);
  or or_2 (or_2_out, Clr, rst_d);
  D_Flip_Flop #(.trigger("falling")) d_ff_1 (
    .clk(and_1_out), .D(d_ff_1_qn), .Q(Qcc), .Qn(d_ff_1_qn), .preset(1'b0), .reset(or_2_out));
endmodule

module _0_11_counter_test (
  input  in_1
);

  wire clock_1_out;
  wire [3:0] n0_11_counter_1_i;

  Clock clock_1 (.out(clock_1_out));
  Hex_Digit_Display hex_digit_display_1 (.value(n0_11_counter_1_i), .dp(1'b0));
  _0_11_counter u_0_11_counter_1 (
    .Clr(1'b0), .Adj(in_1), .Cpu(clock_1_out), .Cpd(1'b0), .i(n0_11_counter_1_i), .rst_d(1'b0));  // open: Qcc, out_7
endmodule

module _1to5 (
  input  in_1,
  output [4:0] out_2
);


  assign out_2 = {5{in_1}};
endmodule

module _4to5 (
  input  [3:0] in_1,
  output [4:0] out_2
);


  assign out_2 = {1'b0, in_1};
endmodule

module _5bits2BCD (
  input  e,
  input  d,
  input  c,
  input  b,
  input  a,
  output h3,
  output h2,
  output h1,
  output h0,
  output b3,
  output b2,
  output b1,
  output b0
);

  wire and_1_out, and_2_out, and_3_out, and_4_out, and_5_out, and_6_out, and_7_out, and_8_out, and_9_out,
       and_10_out, and_11_out, and_12_out, and_13_out, and_14_out, and_15_out, and_16_out, and_17_out,
       and_18_out, not_1_out, not_2_out, not_3_out, not_4_out, not_5_out, not_6_out, not_7_out, not_8_out,
       not_9_out, not_10_out, not_11_out, not_12_out, not_13_out, not_14_out, not_15_out, not_16_out,
       not_17_out, not_18_out, not_19_out, not_20_out, not_21_out, not_22_out, not_23_out, not_24_out,
       not_25_out;

  and and_1 (and_1_out, e, c);
  and and_2 (and_2_out, e, d);
  not not_1 (not_1_out, e);
  not not_2 (not_2_out, e);
  not not_3 (not_3_out, d);
  not not_4 (not_4_out, c);
  not not_5 (not_5_out, e);
  not not_6 (not_6_out, c);
  not not_7 (not_7_out, b);
  not not_8 (not_8_out, d);
  not not_9 (not_9_out, c);
  not not_10 (not_10_out, b);
  not not_11 (not_11_out, e);
  not not_12 (not_12_out, d);
  not not_13 (not_13_out, e);
  not not_14 (not_14_out, c);
  not not_15 (not_15_out, b);
  not not_16 (not_16_out, c);
  not not_17 (not_17_out, e);
  not not_18 (not_18_out, d);
  not not_19 (not_19_out, d);
  not not_20 (not_20_out, e);
  not not_21 (not_21_out, b);
  not not_22 (not_22_out, d);
  not not_23 (not_23_out, c);
  not not_24 (not_24_out, b);
  not not_25 (not_25_out, c);
  or or_1 (h1, and_1_out, and_2_out);
  and and_3 (and_3_out, not_1_out, d, b);
  and and_4 (and_4_out, not_2_out, d, c);
  and and_5 (and_5_out, d, c, b);
  and and_6 (and_6_out, e, not_3_out, not_4_out);
  and and_7 (and_7_out, not_5_out, d, not_6_out, not_7_out);
  and and_8 (and_8_out, e, not_8_out, not_9_out, b);
  and and_9 (and_9_out, e, d, c, not_10_out);
  and and_10 (and_10_out, not_11_out, not_12_out, c);
  and and_11 (and_11_out, not_13_out, c, b);
  and and_12 (and_12_out, e, not_14_out, not_15_out);
  and and_13 (and_13_out, e, d, not_16_out);
  and and_14 (and_14_out, not_17_out, not_18_out, b);
  and and_15 (and_15_out, not_19_out, c, b);
  and and_16 (and_16_out, not_20_out, d, c, not_21_out);
  and and_17 (and_17_out, e, not_22_out, not_23_out, not_24_out);
  and and_18 (and_18_out, e, d, not_25_out, b);
  or or_2 (h0, and_3_out, and_4_out, and_5_out, and_6_out);
  or or_3 (b3, and_7_out, and_8_out, and_9_out);
  or or_4 (b2, and_10_out, and_11_out, and_12_out, and_13_out);
  or or_5 (b1, and_14_out, and_15_out, and_16_out, and_17_out, and_18_out);

  assign b0 = a;
  assign h2 = 1'b0;
  assign h3 = 1'b0;
endmodule

module _5bits2BCD_test (
);

  wire clock_1_out;
  wire [3:0] n5bits2bcd_1_b0, n5bits2bcd_1_h0;
  wire [4:0] counter_1_q, n1to5_1_out_2;

  Counter #(.width(5), .max('h1f)) counter_1 (
    .load(1'b0), .D(n1to5_1_out_2), .count(1'b1), .Q(counter_1_q), .clk(clock_1_out), .clr(1'b0),
    .preset(1'b0), .down(1'b0));  // open: carry
  _1to5 u_1to5_1 (.in_1(1'b0), .out_2(n1to5_1_out_2));
  Clock clock_1 (.out(clock_1_out));
  Hex_Digit_Display hex_digit_display_1 (.value(n5bits2bcd_1_h0), .dp(1'b0));
  _5bits2BCD u_5bits2bcd_1 (
    .e(counter_1_q[4]), .h3(n5bits2bcd_1_h0[3]), .d(counter_1_q[3]), .h2(n5bits2bcd_1_h0[2]),
    .c(counter_1_q[2]), .h1(n5bits2bcd_1_h0[1]), .b(counter_1_q[1]), .a(counter_1_q[0]),
    .h0(n5bits2bcd_1_h0[0]), .b3(n5bits2bcd_1_b0[3]), .b2(n5bits2bcd_1_b0[2]), .b1(n5bits2bcd_1_b0[1]),
    .b0(n5bits2bcd_1_b0[0]));
  Hex_Digit_Display hex_digit_display_2 (.value(n5bits2bcd_1_b0), .dp(1'b0));
endmodule

module led_base (
  input  in_1,
  input  in_2,
  input  in_3,
  input  in_4,
  output [3:0] out_5
);


  assign out_5 = {in_4, in_3, in_2, in_1};
endmodule

module mini_d_ff (
  input  in_1,
  input  in_2,
  output out_3
);

  wire d_ff_1_qn;

  D_Flip_Flop #(.trigger("falling")) d_ff_1 (
    .clk(in_1), .D(d_ff_1_qn), .Q(out_3), .Qn(d_ff_1_qn), .preset(1'b0), .reset(in_2));
endmodule

module hour_fix (
  input  H3,
  input  H2,
  input  H1,
  input  H0,
  input  L3,
  input  L2,
  input  L1,
  input  L0,
  input  nSet,
  output [3:0] L,
  output [3:0] H
);

  wire and_1_out, nor_1_out;
  wire [3:0] led_base_1_out_5, led_base_2_out_5;

  // Probe on led_base_1_out_5
  led_base led_base_1 (.in_1(H0), .in_2(H1), .in_3(H2), .in_4(H3), .out_5(led_base_1_out_5));
  // Probe on led_base_2_out_5
  led_base led_base_2 (.in_1(L0), .in_2(L1), .in_3(L2), .in_4(L3), .out_5(led_base_2_out_5));
  nor nor_1 (nor_1_out, led_base_1_out_5[0], led_base_1_out_5[1], led_base_1_out_5[2], led_base_1_out_5[3], led_base_2_out_5[0], led_base_2_out_5[1], led_base_2_out_5[2], led_base_2_out_5[3]);
  Multiplexer #(.width(8), .enable("false")) multiplexer_1 (
    .in0({led_base_1_out_5, led_base_2_out_5}), .in1(8'h12), .out({H, L}), .sel(and_1_out));
  // Probe on {H, L}
  and and_1 (and_1_out, nor_1_out, nSet);
endmodule

module _1_12_counter (
  input  Adj,
  input  rst_d,
  input  Cpu,
  input  Clr,
  input  Cpd,
  output [3:0] i,
  output out_7,
  output Qcc
);

  wire and_1_out, and_2_out, d_ff_1_qn, nand_1_out, not_1_out, not_2_out, or_1_out, or_2_out;
  wire [3:0] L_q_a, multiplexer_1_out;

  nand nand_1 (nand_1_out, Adj, Cpd);
  not not_1 (not_1_out, Cpu);
  or or_1 (or_1_out, and_1_out, Clr);
  nor nor_1 (out_7, L_q_a[3], L_q_a[2], L_q_a[1], L_q_a[0]);
  Multiplexer #(.width(4), .enable("false")) multiplexer_1 (
    .in0(4'b0000), .in1(4'b1011), .out(multiplexer_1_out), .sel(and_2_out));
  \四位二进制可逆计数器  L (
    .CP_D(nand_1_out), .nLD(not_2_out), .A(multiplexer_1_out[0]), .CLR(or_1_out), .B(multiplexer_1_out[1]),
    .C(multiplexer_1_out[2]), .D(multiplexer_1_out[3]), .Q_A(L_q_a[0]), .Q_B(L_q_a[1]), .Q_C(L_q_a[2]),
    .Q_D(L_q_a[3]), .CP_U(not_1_out));
  // Probe on i
  Adder #(.width(4)) adder_1 (.a(4'b0001), .b(L_q_a), .out(i), .cin(1'b0));  // open: cout
  and and_1 (and_1_out, L_q_a[3], L_q_a[2], ~L_q_a[1], ~L_q_a[0]);  // AND_Gate
  and and_2 (and_2_out, L_q_a[3], L_q_a[2], L_q_a[1], L_q_a[0]);
  not not_2 (not_2_out, and_2_out);
  or or_2 (or_2_out, Clr, rst_d);
  D_Flip_Flop #(.trigger("falling")) d_ff_1 (
    .clk(and_1_out), .D(d_ff_1_qn), .Q(Qcc), .Qn(d_ff_1_qn), .preset(1'b0), .reset(or_2_out));
endmodule
