// Logisim project lab6.circ as structural Verilog: 8 circuits, main circuit sqrX
module sqrX (
  input  [31:0] a,
  input  [31:0] b,
  input  [31:0] c,
  input  [31:0] d,
  output [31:0] a_prime,
  output [31:0] b_prime,
  output [31:0] c_prime,
  output [31:0] d_prime
);

  wire adder_1_cout, adder_2_cout, adder_3_cout;
  wire [31:0] multiplier_1_cout, multiplier_1_out, multiplier_2_cout, multiplier_2_out, multiplier_3_cout,
       multiplier_3_out, multiplier_4_cout, multiplier_4_out, multiplier_5_cout, multiplier_5_out,
       multiplier_6_cout, multiplier_6_out, multiplier_7_out;

  Multiplier #(.width(32)) multiplier_1 (
    .a(a), .b(a), .out(multiplier_1_out), .cin({32{1'b0}}), .cout(multiplier_1_cout));
  Multiplier #(.width(32)) multiplier_2 (
    .a(a), .b(b), .out(multiplier_2_out), .cin(multiplier_1_cout), .cout(multiplier_2_cout));
  Multiplier #(.width(32)) multiplier_3 (
    .a(a), .b(c), .out(multiplier_3_out), .cin(multiplier_2_cout), .cout(multiplier_3_cout));
  Multiplier #(.width(32)) multiplier_4 (
    .a(b), .b(c), .out(multiplier_4_out), .cin(multiplier_3_cout), .cout(multiplier_4_cout));
  Multiplier #(.width(32)) multiplier_5 (
    .a(b), .b(d), .out(multiplier_5_out), .cin(multiplier_4_cout), .cout(multiplier_5_cout));
  Multiplier #(.width(32)) multiplier_6 (
    .a(c), .b(d), .out(multiplier_6_out), .cin(multiplier_5_cout), .cout(multiplier_6_cout));
  Multiplier #(.width(32)) multiplier_7 (.a(d), .b(d), .out(multiplier_7_out), .cin(multiplier_6_cout));  // open: cout
  Adder #(.width(32)) adder_1 (
    .a(multiplier_1_out), .b(multiplier_4_out), .out(a_prime), .cin(1'b0), .cout(adder_1_cout));
  Adder #(.width(32)) adder_2 (
    .a(multiplier_2_out), .b(multiplier_5_out), .out(b_prime), .cin(adder_1_cout), .cout(adder_2_cout));
  Adder #(.width(32)) adder_3 (
    .a(multiplier_3_out), .b(multiplier_6_out), .out(c_prime), .cin(adder_2_cout), .cout(adder_3_cout));
  Adder #(.width(32)) adder_4 (
    .a(multiplier_4_out), .b(multiplier_7_out), .out(d_prime), .cin(adder_3_cout));  // open: cout
endmodule

module sqrX_A (
  input  [31:0] a,
  input  [31:0] b,
  input  [31:0] c,
  input  [31:0] d,
  output [31:0] a_prime_prime,
  output [31:0] b_prime_prime,
  output [31:0] c_prime_prime,
  output [31:0] d_prime_prime
);

  wire [31:0] sqrx_1_a_prime, sqrx_1_c_prime;

  sqrX sqrx_1 (
    .a(a), .b(b), .c(c), .d(d), .a_prime(sqrx_1_a_prime), .b_prime(a_prime_prime), .c_prime(sqrx_1_c_prime),
    .d_prime(c_prime_prime));
  Adder #(.width(32)) adder_1 (.a(sqrx_1_a_prime), .b(a_prime_prime), .out(b_prime_prime), .cin(1'b0));  // open: cout
  Adder #(.width(32)) adder_2 (.a(sqrx_1_c_prime), .b(c_prime_prime), .out(d_prime_prime), .cin(1'b0));  // open: cout
endmodule

module Fibo (
  input  start,
  input  clk,
  input  clr,
  input  ni_1,
  output [31:0] Fn
);

  wire and_1_out, buffer_1_out, buffer_2_out, buffer_3_out, d_ff_1_q, or_1_out;
  wire [31:0] multiplexer_1_out, multiplexer_2_out, multiplexer_3_out, multiplexer_4_out, multiplexer_6_out,
       multiplexer_7_out, multiplexer_8_out, multiplexer_9_out, register_1_q, register_2_q, register_3_q,
       register_4_q, sqrx_1_a_prime, sqrx_1_b_prime, sqrx_1_c_prime, sqrx_1_d_prime, sqrx_a_1_a_prime_prime,
       sqrx_a_1_b_prime_prime, sqrx_a_1_c_prime_prime, sqrx_a_1_d_prime_prime;

  Multiplexer #(.width(32), .enable("false")) multiplexer_1 (
    .in0({32{1'b0}}), .in1(multiplexer_6_out), .out(multiplexer_1_out), .sel(and_1_out));
  Multiplexer #(.width(32), .enable("false")) multiplexer_2 (
    .in0(32'h1), .in1(multiplexer_7_out), .out(multiplexer_2_out), .sel(and_1_out));
  Multiplexer #(.width(32), .enable("false")) multiplexer_3 (
    .in0(32'h1), .in1(multiplexer_8_out), .out(multiplexer_3_out), .sel(and_1_out));
  Multiplexer #(.width(32), .enable("false")) multiplexer_4 (
    .in0(32'h1), .in1(multiplexer_9_out), .out(multiplexer_4_out), .sel(and_1_out));
  and and_1 (and_1_out, start, ~clr);  // AND_Gate
  or or_1 (or_1_out, clk, buffer_3_out);
  buf buffer_1 (buffer_1_out, buffer_2_out);
  buf buffer_2 (buffer_2_out, clr);
  Register #(.width(32), .Select("low")) register_1 (
    .D(multiplexer_1_out), .en(1'b1), .Q(register_1_q), .clk(or_1_out), .clr(1'b0), .cs(1'b0), .preset(1'b0));
  Register #(.width(32), .Select("low")) register_2 (
    .D(multiplexer_2_out), .en(1'b1), .Q(register_2_q), .clk(or_1_out), .clr(1'b0), .cs(1'b0), .preset(1'b0));
  Register #(.width(32), .Select("low")) register_3 (
    .D(multiplexer_3_out), .en(1'b1), .Q(register_3_q), .clk(or_1_out), .clr(1'b0), .cs(1'b0), .preset(1'b0));
  Register #(.width(32), .Select("low")) register_4 (
    .D(multiplexer_4_out), .en(1'b1), .Q(register_4_q), .clk(or_1_out), .clr(1'b0), .cs(1'b0), .preset(1'b0));
  buf buffer_3 (buffer_3_out, buffer_1_out);
  sqrX sqrx_1 (
    .a(register_1_q), .b(register_2_q), .c(register_3_q), .d(register_4_q), .a_prime(sqrx_1_a_prime),
    .b_prime(sqrx_1_b_prime), .c_prime(sqrx_1_c_prime), .d_prime(sqrx_1_d_prime));
  sqrX_A sqrx_a_1 (
    .a(register_1_q), .b(register_2_q), .c(register_3_q), .d(register_4_q),
    .a_prime_prime(sqrx_a_1_a_prime_prime), .b_prime_prime(sqrx_a_1_b_prime_prime),
    .c_prime_prime(sqrx_a_1_c_prime_prime), .d_prime_prime(sqrx_a_1_d_prime_prime));
  D_Flip_Flop #(.Pre_Clr_Positions("LEGACY"), .enable("true")) d_ff_1 (
    .clk(clk), .D(start), .Q(d_ff_1_q), .preset(1'b0), .en(1'b1), .reset(1'b0));  // open: Qn
  Multiplexer #(.width(32), .enable("false")) multiplexer_5 (
    .in0({32{1'b0}}), .in1(register_2_q), .out(Fn), .sel(d_ff_1_q));
  Multiplexer #(.width(32), .enable("false")) multiplexer_6 (
    .in0(sqrx_1_a_prime), .in1(sqrx_a_1_a_prime_prime), .out(multiplexer_6_out), .sel(ni_1));
  Multiplexer #(.width(32), .enable("false")) multiplexer_7 (
    .in0(sqrx_1_b_prime), .in1(sqrx_a_1_b_prime_prime), .out(multiplexer_7_out), .sel(ni_1));
  Multiplexer #(.width(32), .enable("false")) multiplexer_8 (
    .in0(sqrx_1_c_prime), .in1(sqrx_a_1_c_prime_prime), .out(multiplexer_8_out), .sel(ni_1));
  Multiplexer #(.width(32), .enable("false")) multiplexer_9 (
    .in0(sqrx_1_d_prime), .in1(sqrx_a_1_d_prime_prime), .out(multiplexer_9_out), .sel(ni_1));
endmodule

module \Fibonacci数显示模块  (
  input  [31:0] in_1,
  output [3:0] D0,
  output [3:0] D1,
  output [3:0] D2,
  output [3:0] D3,
  output [3:0] D4,
  output [3:0] D5,
  output [3:0] D6,
  output [3:0] D7,
  output [3:0] D8,
  output [3:0] D9
);

  wire [31:0] divider_1_out, divider_1_rem, divider_2_out, divider_2_rem, divider_3_out, divider_3_rem,
       divider_4_out, divider_4_rem, divider_5_out, divider_5_rem, divider_6_out, divider_6_rem,
       divider_7_out, divider_7_rem, divider_8_out, divider_8_rem, divider_9_rem, divider_10_out,
       divider_10_rem;

  Divider #(.width(32)) divider_1 (.a(in_1), .b(32'ha), .out(divider_1_out), .upper({32{1'b0}}), .rem(divider_1_rem));
  Divider #(.width(32)) divider_2 (
    .a(divider_1_out), .b(32'ha), .out(divider_2_out), .upper({32{1'b0}}), .rem(divider_2_rem));
  _32to4 u_32to4_1 (.in_1(divider_1_rem), .out_2(D0));
  Divider #(.width(32)) divider_3 (
    .a(divider_2_out), .b(32'ha), .out(divider_3_out), .upper({32{1'b0}}), .rem(divider_3_rem));
  _32to4 u_32to4_2 (.in_1(divider_2_rem), .out_2(D1));
  _32to4 u_32to4_3 (.in_1(divider_3_rem), .out_2(D2));
  Divider #(.width(32)) divider_4 (
    .a(divider_3_out), .b(32'ha), .out(divider_4_out), .upper({32{1'b0}}), .rem(divider_4_rem));
  _32to4 u_32to4_4 (.in_1(divider_4_rem), .out_2(D3));
  Divider #(.width(32)) divider_5 (
    .a(divider_4_out), .b(32'ha), .out(divider_5_out), .upper({32{1'b0}}), .rem(divider_5_rem));
  Divider #(.width(32)) divider_6 (
    .a(divider_5_out), .b(32'ha), .out(divider_6_out), .upper({32{1'b0}}), .rem(divider_6_rem));
  _32to4 u_32to4_5 (.in_1(divider_5_rem), .out_2(D4));
  Divider #(.width(32)) divider_7 (
    .a(divider_6_out), .b(32'ha), .out(divider_7_out), .upper({32{1'b0}}), .rem(divider_7_rem));
  _32to4 u_32to4_6 (.in_1(divider_6_rem), .out_2(D5));
  _32to4 u_32to4_7 (.in_1(divider_7_rem), .out_2(D6));
  Divider #(.width(32)) divider_8 (
    .a(divider_7_out), .b(32'ha), .out(divider_8_out), .upper({32{1'b0}}), .rem(divider_8_rem));
  _32to4 u_32to4_8 (.in_1(divider_8_rem), .out_2(D7));
  Divider #(.width(32)) divider_9 (
    .a(divider_10_out), .b(32'ha), .upper({32{1'b0}}), .rem(divider_9_rem));  // open: out
  Divider #(.width(32)) divider_10 (
    .a(divider_8_out), .b(32'ha), .out(divider_10_out), .upper({32{1'b0}}), .rem(divider_10_rem));
  _32to4 u_32to4_9 (.in_1(divider_10_rem), .out_2(D8));
  _32to4 u_32to4_10 (.in_1(divider_9_rem), .out_2(D9));
endmodule

module Controller (
  input  [5:0] n,
  input  clk,
  input  clr,
  output start,
  output clk_2,
  output clear,
  output ni_1
);

  wire and_2_out, comparator_1_gt, d_ff_2_q, or_1_out, shift_register_1_out;
  wire [2:0] counter_1_q;

  Comparator #(.width(3), .mode("unsigned")) comparator_1 (
    .a(3'b110), .b(counter_1_q), .gt(comparator_1_gt));  // open: eq, lt
  Counter #(.width(3), .max('h7), .ongoal("stay")) counter_1 (
    .load(1'b0), .Q(counter_1_q), .clk(clk), .clr(clr), .preset(1'b0), .down(1'b0));  // open: D, count, carry
  and and_1 (clk_2, comparator_1_gt, clk);
  or or_1 (or_1_out, clk_2, clr);
  Shift_Register #(.length(6)) shift_register_1 (
    .clk(or_1_out), .out(shift_register_1_out), .load(clr), .d0(n[0]), .d1(n[1]), .d2(n[2]), .d3(n[3]),
    .d4(n[4]), .d5(n[5]));  // open: shift, in, clr, q0, q1, q2, q3, q4, q5
  and and_2 (and_2_out, shift_register_1_out, ~clr);  // AND_Gate
  D_Flip_Flop d_ff_1 (.clk(and_2_out), .D(1'b1), .Q(start), .preset(1'b0), .reset(clr));  // open: Qn
  D_Flip_Flop d_ff_2 (.clk(clk_2), .D(start), .Q(d_ff_2_q), .preset(1'b0), .reset(clr));  // open: Qn
  Multiplexer #(.enable("false")) multiplexer_1 (.in1(shift_register_1_out), .out(ni_1), .sel(d_ff_2_q));  // open: in0

  assign clear = clr;
endmodule

module \Fibonacci数列计算器  (
  input  [5:0] in_1,
  input  in_2,
  input  in_3,
  output [3:0] out_4,
  output [3:0] out_5,
  output [3:0] out_6,
  output [3:0] out_7,
  output [3:0] out_8,
  output [3:0] out_9,
  output [3:0] out_10,
  output [3:0] out_11,
  output [3:0] out_12,
  output [3:0] out_13
);

  wire controller_1_clear, controller_1_clk_2, controller_1_ni_1, controller_1_start;
  wire [31:0] fibo_1_fn;

  Controller controller_1 (
    .n(in_1), .clk(in_3), .clr(in_2), .start(controller_1_start), .clk_2(controller_1_clk_2),
    .clear(controller_1_clear), .ni_1(controller_1_ni_1));
  Fibo fibo_1 (
    .start(controller_1_start), .clk(controller_1_clk_2), .clr(controller_1_clear), .ni_1(controller_1_ni_1),
    .Fn(fibo_1_fn));
  \Fibonacci数显示模块  \fibonacci数显示模块_1  (
    .in_1(fibo_1_fn), .D0(out_13), .D1(out_12), .D2(out_11), .D3(out_10), .D4(out_9), .D5(out_8), .D6(out_7),
    .D7(out_6), .D8(out_5), .D9(out_4));
endmodule

module \Fibonacci数列计算器测试电路  (
  input  [5:0] in_1
);

  wire button_1_out, clock_1_out;
  wire [3:0] \fibonacci数列计算器_1_out_4 , \fibonacci数列计算器_1_out_5 , \fibonacci数列计算器_1_out_6 ,
       \fibonacci数列计算器_1_out_7 , \fibonacci数列计算器_1_out_8 , \fibonacci数列计算器_1_out_9 ,
       \fibonacci数列计算器_1_out_10 , \fibonacci数列计算器_1_out_11 , \fibonacci数列计算器_1_out_12 ,
       \fibonacci数列计算器_1_out_13 ;

  Hex_Digit_Display hex_digit_display_1 (.value(\fibonacci数列计算器_1_out_4 ));  // open: dp
  \Fibonacci数列计算器  \fibonacci数列计算器_1  (
    .in_1(in_1), .in_2(button_1_out), .in_3(clock_1_out), .out_4(\fibonacci数列计算器_1_out_4 ),
    .out_5(\fibonacci数列计算器_1_out_5 ), .out_6(\fibonacci数列计算器_1_out_6 ), .out_7(\fibonacci数列计算器_1_out_7 ),
    .out_8(\fibonacci数列计算器_1_out_8 ), .out_9(\fibonacci数列计算器_1_out_9 ), .out_10(\fibonacci数列计算器_1_out_10 ),
    .out_11(\fibonacci数列计算器_1_out_11 ), .out_12(\fibonacci数列计算器_1_out_12 ), .out_13(\fibonacci数列计算器_1_out_13 ));
  Hex_Digit_Display hex_digit_display_2 (.value(\fibonacci数列计算器_1_out_5 ));  // open: dp
  Hex_Digit_Display hex_digit_display_3 (.value(\fibonacci数列计算器_1_out_6 ));  // open: dp
  Button button_1 (.out(button_1_out));
  Hex_Digit_Display hex_digit_display_4 (.value(\fibonacci数列计算器_1_out_8 ));  // open: dp
  Hex_Digit_Display hex_digit_display_5 (.value(\fibonacci数列计算器_1_out_7 ));  // open: dp
  Clock clock_1 (.out(clock_1_out));
  Hex_Digit_Display hex_digit_display_6 (.value(\fibonacci数列计算器_1_out_10 ));  // open: dp
  Hex_Digit_Display hex_digit_display_7 (.value(\fibonacci数列计算器_1_out_9 ));  // open: dp
  Hex_Digit_Display hex_digit_display_8 (.value(\fibonacci数列计算器_1_out_11 ));  // open: dp
  Hex_Digit_Display hex_digit_display_9 (.value(\fibonacci数列计算器_1_out_12 ));  // open: dp
  Hex_Digit_Display hex_digit_display_10 (.value(\fibonacci数列计算器_1_out_13 ));  // open: dp
endmodule

module _32to4 (
  input  [31:0] in_1,
  output [3:0] out_2
);


  assign out_2 = in_1[3:0];
endmodule
